// Logisim project CPU.circ as structural Verilog: 14 circuits, main circuit main
module main (
  input  in_1,
  input  [7:0] in_2,
  input  in_3,
  input  in_4,
  input  in_5,
  input  in_6,
  input  in_7,
  input  in_8,
  input  in_9,
  input  in_10,
  input  in_11,
  input  in_12
);

  wire and_1_out, and_2_out, and_3_out, and_4_out, and_5_out, and_6_out, clock_1_out, cu_1_alu_exe,
       cu_1_alu_flag, cu_1_alu_l, cu_1_alu_o, cu_1_alu_r, cu_1_ar_in, cu_1_branch_sign, cu_1_dr_in,
       cu_1_dr_out, cu_1_inpt, cu_1_ir, cu_1_mar_in, cu_1_mar_out, cu_1_mbr_in, cu_1_mbr_out, cu_1_pc_a_i,
       cu_1_pc_inc, cu_1_pc_out, cu_1_pnt, cu_1_r_w, cu_1_ram_r, cu_1_ram_w, cu_1_reg0, cu_1_reg1, cu_1_stat,
       not_1_out, not_2_out, not_3_out, not_4_out, or_1_out, or_2_out, or_3_out;
  wire [6:0] display_1_out_2, display_1_out_3, display_1_out_4;
  wire [7:0] ADDR_o, alu_1_flags, alu_1_o, buffer_1_out, buffer_4_out, controlled_buffer_1_out, cu_1_pc_a_o,
       cu_1_ram_a, DATA_o, general_reg_1_o, general_reg_2_o, incby1_1_to_pc, input_buffer_1_out_11, MAR_o,
       MBR_o, mode_reg_1_o, multiplexer_1_out, R0_o, R1_o;

  Clock clock_1 (.out(clock_1_out));
  GENERAL_REG DATA (.I(controlled_buffer_1_out), .O(DATA_o), .in_2(cu_1_dr_in));
  RAM_16bytes ram_16bytes_1 (
    .in_3(mode_reg_1_o), .in_4(controlled_buffer_1_out), .in_2(ADDR_o), .data_output(DATA_o),
    .clk(clock_1_out));
  GENERAL_REG ADDR (.I(controlled_buffer_1_out), .O(ADDR_o), .in_2(cu_1_ar_in));
  or or_1 (or_1_out, cu_1_ram_w, cu_1_ram_r);
  assign controlled_buffer_1_out = cu_1_inpt ? input_buffer_1_out_11 : 8'bz;  // Controlled_Buffer controlled_buffer_1
  INPUT_BUFFER input_buffer_1 (
    .in_5(in_7), .in_2(in_4), .in_4(in_6), .in_3(in_5), .in_7(in_9), .in_8(in_10),
    .out_11(input_buffer_1_out_11), .in_6(in_8), .in_1(in_3), .in_9(in_11), .in_10(in_12));
  GENERAL_REG general_reg_1 (.I(controlled_buffer_1_out), .O(general_reg_1_o), .in_2(cu_1_pnt));
  MODE_REG mode_reg_1 (.O(mode_reg_1_o), .in_2(or_1_out), .I(cu_1_ram_w));
  DISPLAY display_1 (.out_4(display_1_out_4), .out_3(display_1_out_3), .in_1(general_reg_1_o), .out_2(display_1_out_2));
  assign controlled_buffer_1_out = cu_1_dr_out ? DATA_o : 8'bz;  // Controlled_Buffer controlled_buffer_2
  _7_Segment_Display u_7_segment_display_1 (
    .g(display_1_out_2[6]), .f(display_1_out_2[5]), .a(display_1_out_2[0]), .b(display_1_out_2[1]),
    .e(display_1_out_2[4]), .d(display_1_out_2[3]), .c(display_1_out_2[2]));  // open: dp
  assign buffer_1_out = controlled_buffer_1_out;  // Buffer buffer_1, 8 bits wide
  assign buffer_1_out = controlled_buffer_1_out;  // Buffer buffer_2, 8 bits wide
  assign buffer_1_out = buffer_4_out;  // Buffer buffer_3, 8 bits wide
  _7_Segment_Display u_7_segment_display_2 (
    .g(display_1_out_3[6]), .f(display_1_out_3[5]), .a(display_1_out_3[0]), .b(display_1_out_3[1]),
    .e(display_1_out_3[4]), .d(display_1_out_3[3]), .c(display_1_out_3[2]));  // open: dp
  assign controlled_buffer_1_out = cu_1_mar_out ? MAR_o : 8'bz;  // Controlled_Buffer controlled_buffer_3
  GENERAL_REG MAR (.I(buffer_1_out), .O(MAR_o), .in_2(cu_1_mar_in));
  GENERAL_REG MBR (.I(buffer_1_out), .O(MBR_o), .in_2(cu_1_mbr_in));
  _7_Segment_Display u_7_segment_display_3 (
    .g(display_1_out_4[6]), .f(display_1_out_4[5]), .a(display_1_out_4[0]), .b(display_1_out_4[1]),
    .e(display_1_out_4[4]), .d(display_1_out_4[3]), .c(display_1_out_4[2]));  // open: dp
  assign buffer_4_out = controlled_buffer_1_out;  // Buffer buffer_4, 8 bits wide
  assign buffer_4_out = controlled_buffer_1_out;  // Buffer buffer_5, 8 bits wide
  assign controlled_buffer_1_out = cu_1_mbr_out ? MBR_o : 8'bz;  // Controlled_Buffer controlled_buffer_4
  and and_1 (and_1_out, cu_1_pc_a_i, not_1_out, cu_1_branch_sign);
  not not_1 (not_1_out, buffer_4_out[0]);
  and and_2 (and_2_out, cu_1_pc_a_i, buffer_4_out[0], not_2_out);
  not not_2 (not_2_out, cu_1_branch_sign);
  INCBY1 incby1_1 (.from_PC(general_reg_2_o), .to_PC(incby1_1_to_pc));
  Multiplexer #(.width(8), .enable("false")) multiplexer_1 (
    .in0(incby1_1_to_pc), .in1(cu_1_pc_a_o), .out(multiplexer_1_out), .sel(or_2_out));
  or or_2 (or_2_out, and_1_out, and_2_out);
  GENERAL_REG general_reg_2 (.I(multiplexer_1_out), .O(general_reg_2_o), .in_2(or_3_out));
  or or_3 (or_3_out, cu_1_pc_inc, or_2_out);
  assign buffer_4_out = and_3_out ? R0_o : 8'bz;  // Controlled_Buffer controlled_buffer_5
  GENERAL_REG R0 (.I(buffer_4_out), .O(R0_o), .in_2(and_4_out));
  not not_3 (not_3_out, cu_1_r_w);
  and and_3 (and_3_out, not_3_out, cu_1_reg0);
  and and_4 (and_4_out, cu_1_reg0, cu_1_r_w);
  assign buffer_4_out = cu_1_pc_out ? general_reg_2_o : 8'bz;  // Controlled_Buffer controlled_buffer_6
  GENERAL_REG general_reg_3 (.I(buffer_4_out), .in_2(cu_1_ir));  // open: O
  assign buffer_4_out = and_5_out ? R1_o : 8'bz;  // Controlled_Buffer controlled_buffer_7
  GENERAL_REG R1 (.I(buffer_4_out), .O(R1_o), .in_2(and_6_out));
  not not_4 (not_4_out, cu_1_r_w);
  and and_5 (and_5_out, not_4_out, cu_1_reg1);
  and and_6 (and_6_out, cu_1_reg1, cu_1_r_w);
  ALU alu_1 (
    .O(alu_1_o), .L(buffer_4_out), .R(buffer_4_out), .Mode(cu_1_alu_flag), .Flags(alu_1_flags),
    .R_W(cu_1_alu_r), .L_W(cu_1_alu_l), .ALU_ACTV(cu_1_alu_exe));
  assign buffer_4_out = cu_1_alu_o ? alu_1_o : 8'bz;  // Controlled_Buffer controlled_buffer_8
  assign buffer_4_out = cu_1_stat ? alu_1_flags : 8'bz;  // Controlled_Buffer controlled_buffer_9
  CU cu_1 (
    .MBR_OUT(cu_1_mbr_out), .DR_OUT(cu_1_dr_out), .RAM_R(cu_1_ram_r), .PC_INC(cu_1_pc_inc),
    .AR_IN(cu_1_ar_in), .PC_OUT(cu_1_pc_out), .ALU_O(cu_1_alu_o), .R_W(cu_1_r_w), .ALU_R(cu_1_alu_r),
    .MAR_IN(cu_1_mar_in), .PC_A_I(cu_1_pc_a_i), .IRin(in_2), .ALU_FLAG(cu_1_alu_flag), .Reg0(cu_1_reg0),
    .DR_IN(cu_1_dr_in), .Reg1(cu_1_reg1), .ALU_EXE(cu_1_alu_exe), .MBR_IN(cu_1_mbr_in), .ALU_L(cu_1_alu_l),
    .BRANCH_SIGN(cu_1_branch_sign), .STAT(cu_1_stat), .MAR_OUT(cu_1_mar_out), .RAM_W(cu_1_ram_w),
    .RAM_A(cu_1_ram_a), .PC_A_O(cu_1_pc_a_o), .Initial_On_Keep_On(in_1), .IR(cu_1_ir), .PNT(cu_1_pnt),
    .INPT(cu_1_inpt));
  // Probe on buffer_4_out

  // Notes on the sheet:
  //   CPU BUS
endmodule

module mem_cell (
  input  \input ,
  input  mode,
  input  select,
  input  in_4,
  output \output 
);

  wire and_1_out, and_2_out, not_1_out, not_2_out, s_r_ff_1_q;

  and and_1 (and_1_out, mode, select, not_1_out);
  not not_1 (not_1_out, \input );
  S_R_Flip_Flop s_r_ff_1 (.S(and_2_out), .R(and_1_out), .clk(in_4), .Q(s_r_ff_1_q));  // open: reset, Qn, preset
  and and_2 (and_2_out, \input , mode, select);
  not not_2 (not_2_out, mode);
  and and_3 (\output , s_r_ff_1_q, not_2_out, select);

  // Notes on the sheet:
  //   clk
endmodule

module RAM_16bytes (
  input  clk,
  input  [7:0] in_2,
  input  [7:0] in_3,
  input  [7:0] in_4,
  output [7:0] data_output
);

  wire A0000_out, A0001_out, A0010_out, A0011_out, A0100_out, A0101_out, A0110_out, A0111_out, A111_out,
       A1000_out, A1001_out, A1010_out, A1011_out, A1100_out, A1101_out, A1110_out, mem_cell_1_output,
       mem_cell_2_output, mem_cell_3_output, mem_cell_4_output, mem_cell_5_output, mem_cell_6_output,
       mem_cell_7_output, mem_cell_8_output, mem_cell_9_output, mem_cell_10_output, mem_cell_11_output,
       mem_cell_12_output, mem_cell_13_output, mem_cell_14_output, mem_cell_15_output, mem_cell_16_output,
       mem_cell_17_output, mem_cell_18_output, mem_cell_19_output, mem_cell_20_output, mem_cell_21_output,
       mem_cell_22_output, mem_cell_23_output, mem_cell_24_output, mem_cell_25_output, mem_cell_26_output,
       mem_cell_27_output, mem_cell_28_output, mem_cell_29_output, mem_cell_30_output, mem_cell_31_output,
       mem_cell_32_output, mem_cell_33_output, mem_cell_34_output, mem_cell_35_output, mem_cell_36_output,
       mem_cell_37_output, mem_cell_38_output, mem_cell_39_output, mem_cell_40_output, mem_cell_41_output,
       mem_cell_42_output, mem_cell_43_output, mem_cell_44_output, mem_cell_45_output, mem_cell_46_output,
       mem_cell_47_output, mem_cell_48_output, mem_cell_49_output, mem_cell_50_output, mem_cell_51_output,
       mem_cell_52_output, mem_cell_53_output, mem_cell_54_output, mem_cell_55_output, mem_cell_56_output,
       mem_cell_57_output, mem_cell_58_output, mem_cell_59_output, mem_cell_60_output, mem_cell_61_output,
       mem_cell_62_output, mem_cell_63_output, mem_cell_64_output, mem_cell_65_output, mem_cell_66_output,
       mem_cell_67_output, mem_cell_68_output, mem_cell_69_output, mem_cell_70_output, mem_cell_71_output,
       mem_cell_72_output, mem_cell_73_output, mem_cell_74_output, mem_cell_75_output, mem_cell_76_output,
       mem_cell_77_output, mem_cell_78_output, mem_cell_79_output, mem_cell_80_output, mem_cell_81_output,
       mem_cell_82_output, mem_cell_83_output, mem_cell_84_output, mem_cell_85_output, mem_cell_86_output,
       mem_cell_87_output, mem_cell_88_output, mem_cell_89_output, mem_cell_90_output, mem_cell_91_output,
       mem_cell_92_output, mem_cell_93_output, mem_cell_94_output, mem_cell_95_output, mem_cell_96_output,
       mem_cell_97_output, mem_cell_98_output, mem_cell_99_output, mem_cell_100_output, mem_cell_101_output,
       mem_cell_102_output, mem_cell_103_output, mem_cell_104_output, mem_cell_105_output,
       mem_cell_106_output, mem_cell_107_output, mem_cell_108_output, mem_cell_109_output,
       mem_cell_110_output, mem_cell_111_output, mem_cell_112_output, mem_cell_113_output,
       mem_cell_114_output, mem_cell_115_output, mem_cell_116_output, mem_cell_117_output,
       mem_cell_118_output, mem_cell_119_output, mem_cell_120_output, mem_cell_121_output,
       mem_cell_122_output, mem_cell_123_output, mem_cell_124_output, mem_cell_125_output,
       mem_cell_126_output, mem_cell_127_output, mem_cell_128_output, not_1_out, not_2_out, not_3_out,
       not_4_out, or_1_out, or_2_out, or_3_out, or_4_out, or_5_out, or_6_out, or_7_out, or_8_out, or_9_out,
       or_10_out, or_11_out, or_12_out, or_13_out, or_14_out, or_15_out, or_16_out, or_17_out, or_18_out,
       or_19_out, or_20_out, or_21_out, or_22_out, or_23_out, or_24_out;

  not not_1 (not_1_out, in_2[2]);
  not not_2 (not_2_out, in_2[0]);
  not not_3 (not_3_out, in_2[1]);
  not not_4 (not_4_out, in_2[3]);
  and A0000 (A0000_out, not_4_out, not_1_out, not_3_out, not_2_out);
  mem_cell mem_cell_1 (.\input (in_4[0]), .mode(in_3[0]), .select(A0000_out), .\output (mem_cell_1_output), .in_4(clk));
  mem_cell mem_cell_2 (.\input (in_4[1]), .mode(in_3[0]), .select(A0000_out), .\output (mem_cell_2_output), .in_4(clk));
  mem_cell mem_cell_3 (.\input (in_4[2]), .mode(in_3[0]), .select(A0000_out), .\output (mem_cell_3_output), .in_4(clk));
  mem_cell mem_cell_4 (.\input (in_4[3]), .mode(in_3[0]), .select(A0000_out), .\output (mem_cell_4_output), .in_4(clk));
  mem_cell mem_cell_5 (.\input (in_4[4]), .mode(in_3[0]), .select(A0000_out), .\output (mem_cell_5_output), .in_4(clk));
  mem_cell mem_cell_6 (.\input (in_4[5]), .mode(in_3[0]), .select(A0000_out), .\output (mem_cell_6_output), .in_4(clk));
  mem_cell mem_cell_7 (.\input (in_4[6]), .mode(in_3[0]), .select(A0000_out), .\output (mem_cell_7_output), .in_4(clk));
  mem_cell mem_cell_8 (.\input (in_4[7]), .mode(in_3[0]), .select(A0000_out), .\output (mem_cell_8_output), .in_4(clk));
  and A0001 (A0001_out, not_4_out, not_1_out, not_3_out, in_2[0]);
  mem_cell mem_cell_9 (.\input (in_4[0]), .mode(in_3[0]), .select(A0001_out), .\output (mem_cell_9_output), .in_4(clk));
  mem_cell mem_cell_10 (
    .\input (in_4[1]), .mode(in_3[0]), .select(A0001_out), .\output (mem_cell_10_output), .in_4(clk));
  mem_cell mem_cell_11 (
    .\input (in_4[2]), .mode(in_3[0]), .select(A0001_out), .\output (mem_cell_11_output), .in_4(clk));
  mem_cell mem_cell_12 (
    .\input (in_4[3]), .mode(in_3[0]), .select(A0001_out), .\output (mem_cell_12_output), .in_4(clk));
  mem_cell mem_cell_13 (
    .\input (in_4[4]), .mode(in_3[0]), .select(A0001_out), .\output (mem_cell_13_output), .in_4(clk));
  mem_cell mem_cell_14 (
    .\input (in_4[5]), .mode(in_3[0]), .select(A0001_out), .\output (mem_cell_14_output), .in_4(clk));
  mem_cell mem_cell_15 (
    .\input (in_4[6]), .mode(in_3[0]), .select(A0001_out), .\output (mem_cell_15_output), .in_4(clk));
  mem_cell mem_cell_16 (
    .\input (in_4[7]), .mode(in_3[0]), .select(A0001_out), .\output (mem_cell_16_output), .in_4(clk));
  and A0010 (A0010_out, not_4_out, not_1_out, in_2[1], not_2_out);
  mem_cell mem_cell_17 (
    .\input (in_4[0]), .mode(in_3[0]), .select(A0010_out), .\output (mem_cell_17_output), .in_4(clk));
  mem_cell mem_cell_18 (
    .\input (in_4[1]), .mode(in_3[0]), .select(A0010_out), .\output (mem_cell_18_output), .in_4(clk));
  mem_cell mem_cell_19 (
    .\input (in_4[2]), .mode(in_3[0]), .select(A0010_out), .\output (mem_cell_19_output), .in_4(clk));
  mem_cell mem_cell_20 (
    .\input (in_4[3]), .mode(in_3[0]), .select(A0010_out), .\output (mem_cell_20_output), .in_4(clk));
  mem_cell mem_cell_21 (
    .\input (in_4[4]), .mode(in_3[0]), .select(A0010_out), .\output (mem_cell_21_output), .in_4(clk));
  mem_cell mem_cell_22 (
    .\input (in_4[5]), .mode(in_3[0]), .select(A0010_out), .\output (mem_cell_22_output), .in_4(clk));
  mem_cell mem_cell_23 (
    .\input (in_4[6]), .mode(in_3[0]), .select(A0010_out), .\output (mem_cell_23_output), .in_4(clk));
  mem_cell mem_cell_24 (
    .\input (in_4[7]), .mode(in_3[0]), .select(A0010_out), .\output (mem_cell_24_output), .in_4(clk));
  and A0011 (A0011_out, not_4_out, not_1_out, in_2[1], in_2[0]);
  mem_cell mem_cell_25 (
    .\input (in_4[0]), .mode(in_3[0]), .select(A0011_out), .\output (mem_cell_25_output), .in_4(clk));
  mem_cell mem_cell_26 (
    .\input (in_4[1]), .mode(in_3[0]), .select(A0011_out), .\output (mem_cell_26_output), .in_4(clk));
  mem_cell mem_cell_27 (
    .\input (in_4[2]), .mode(in_3[0]), .select(A0011_out), .\output (mem_cell_27_output), .in_4(clk));
  mem_cell mem_cell_28 (
    .\input (in_4[3]), .mode(in_3[0]), .select(A0011_out), .\output (mem_cell_28_output), .in_4(clk));
  mem_cell mem_cell_29 (
    .\input (in_4[4]), .mode(in_3[0]), .select(A0011_out), .\output (mem_cell_29_output), .in_4(clk));
  mem_cell mem_cell_30 (
    .\input (in_4[5]), .mode(in_3[0]), .select(A0011_out), .\output (mem_cell_30_output), .in_4(clk));
  mem_cell mem_cell_31 (
    .\input (in_4[6]), .mode(in_3[0]), .select(A0011_out), .\output (mem_cell_31_output), .in_4(clk));
  mem_cell mem_cell_32 (
    .\input (in_4[7]), .mode(in_3[0]), .select(A0011_out), .\output (mem_cell_32_output), .in_4(clk));
  and A0100 (A0100_out, not_4_out, in_2[2], not_3_out, not_2_out);
  or or_1 (or_1_out, mem_cell_1_output, mem_cell_9_output, mem_cell_17_output, mem_cell_25_output);
  or or_2 (or_2_out, mem_cell_2_output, mem_cell_10_output, mem_cell_18_output, mem_cell_26_output);
  or or_3 (or_3_out, mem_cell_3_output, mem_cell_11_output, mem_cell_19_output, mem_cell_27_output);
  or or_4 (or_4_out, mem_cell_4_output, mem_cell_12_output, mem_cell_20_output, mem_cell_28_output);
  or or_5 (or_5_out, mem_cell_5_output, mem_cell_13_output, mem_cell_21_output, mem_cell_29_output);
  or or_6 (or_6_out, mem_cell_6_output, mem_cell_14_output, mem_cell_22_output, mem_cell_30_output);
  or or_7 (or_7_out, mem_cell_7_output, mem_cell_15_output, mem_cell_23_output, mem_cell_31_output);
  or or_8 (or_8_out, mem_cell_8_output, mem_cell_16_output, mem_cell_24_output, mem_cell_32_output);
  mem_cell mem_cell_33 (
    .\input (in_4[0]), .mode(in_3[0]), .select(A0100_out), .\output (mem_cell_33_output), .in_4(clk));
  mem_cell mem_cell_34 (
    .\input (in_4[1]), .mode(in_3[0]), .select(A0100_out), .\output (mem_cell_34_output), .in_4(clk));
  mem_cell mem_cell_35 (
    .\input (in_4[2]), .mode(in_3[0]), .select(A0100_out), .\output (mem_cell_35_output), .in_4(clk));
  mem_cell mem_cell_36 (
    .\input (in_4[3]), .mode(in_3[0]), .select(A0100_out), .\output (mem_cell_36_output), .in_4(clk));
  mem_cell mem_cell_37 (
    .\input (in_4[4]), .mode(in_3[0]), .select(A0100_out), .\output (mem_cell_37_output), .in_4(clk));
  mem_cell mem_cell_38 (
    .\input (in_4[5]), .mode(in_3[0]), .select(A0100_out), .\output (mem_cell_38_output), .in_4(clk));
  mem_cell mem_cell_39 (
    .\input (in_4[6]), .mode(in_3[0]), .select(A0100_out), .\output (mem_cell_39_output), .in_4(clk));
  mem_cell mem_cell_40 (
    .\input (in_4[7]), .mode(in_3[0]), .select(A0100_out), .\output (mem_cell_40_output), .in_4(clk));
  and A0101 (A0101_out, not_4_out, in_2[2], not_3_out, in_2[0]);
  mem_cell mem_cell_41 (
    .\input (in_4[0]), .mode(in_3[0]), .select(A0101_out), .\output (mem_cell_41_output), .in_4(clk));
  mem_cell mem_cell_42 (
    .\input (in_4[1]), .mode(in_3[0]), .select(A0101_out), .\output (mem_cell_42_output), .in_4(clk));
  mem_cell mem_cell_43 (
    .\input (in_4[2]), .mode(in_3[0]), .select(A0101_out), .\output (mem_cell_43_output), .in_4(clk));
  mem_cell mem_cell_44 (
    .\input (in_4[3]), .mode(in_3[0]), .select(A0101_out), .\output (mem_cell_44_output), .in_4(clk));
  mem_cell mem_cell_45 (
    .\input (in_4[4]), .mode(in_3[0]), .select(A0101_out), .\output (mem_cell_45_output), .in_4(clk));
  mem_cell mem_cell_46 (
    .\input (in_4[5]), .mode(in_3[0]), .select(A0101_out), .\output (mem_cell_46_output), .in_4(clk));
  mem_cell mem_cell_47 (
    .\input (in_4[6]), .mode(in_3[0]), .select(A0101_out), .\output (mem_cell_47_output), .in_4(clk));
  mem_cell mem_cell_48 (
    .\input (in_4[7]), .mode(in_3[0]), .select(A0101_out), .\output (mem_cell_48_output), .in_4(clk));
  and A0110 (A0110_out, not_4_out, in_2[2], in_2[1], not_2_out);
  mem_cell mem_cell_49 (
    .\input (in_4[0]), .mode(in_3[0]), .select(A0110_out), .\output (mem_cell_49_output), .in_4(clk));
  mem_cell mem_cell_50 (
    .\input (in_4[1]), .mode(in_3[0]), .select(A0110_out), .\output (mem_cell_50_output), .in_4(clk));
  mem_cell mem_cell_51 (
    .\input (in_4[2]), .mode(in_3[0]), .select(A0110_out), .\output (mem_cell_51_output), .in_4(clk));
  mem_cell mem_cell_52 (
    .\input (in_4[3]), .mode(in_3[0]), .select(A0110_out), .\output (mem_cell_52_output), .in_4(clk));
  mem_cell mem_cell_53 (
    .\input (in_4[4]), .mode(in_3[0]), .select(A0110_out), .\output (mem_cell_53_output), .in_4(clk));
  mem_cell mem_cell_54 (
    .\input (in_4[5]), .mode(in_3[0]), .select(A0110_out), .\output (mem_cell_54_output), .in_4(clk));
  mem_cell mem_cell_55 (
    .\input (in_4[6]), .mode(in_3[0]), .select(A0110_out), .\output (mem_cell_55_output), .in_4(clk));
  mem_cell mem_cell_56 (
    .\input (in_4[7]), .mode(in_3[0]), .select(A0110_out), .\output (mem_cell_56_output), .in_4(clk));
  and A0111 (A0111_out, not_4_out, in_2[2], in_2[1], in_2[0]);
  mem_cell mem_cell_57 (
    .\input (in_4[0]), .mode(in_3[0]), .select(A0111_out), .\output (mem_cell_57_output), .in_4(clk));
  mem_cell mem_cell_58 (
    .\input (in_4[1]), .mode(in_3[0]), .select(A0111_out), .\output (mem_cell_58_output), .in_4(clk));
  mem_cell mem_cell_59 (
    .\input (in_4[2]), .mode(in_3[0]), .select(A0111_out), .\output (mem_cell_59_output), .in_4(clk));
  mem_cell mem_cell_60 (
    .\input (in_4[3]), .mode(in_3[0]), .select(A0111_out), .\output (mem_cell_60_output), .in_4(clk));
  mem_cell mem_cell_61 (
    .\input (in_4[4]), .mode(in_3[0]), .select(A0111_out), .\output (mem_cell_61_output), .in_4(clk));
  mem_cell mem_cell_62 (
    .\input (in_4[5]), .mode(in_3[0]), .select(A0111_out), .\output (mem_cell_62_output), .in_4(clk));
  mem_cell mem_cell_63 (
    .\input (in_4[6]), .mode(in_3[0]), .select(A0111_out), .\output (mem_cell_63_output), .in_4(clk));
  mem_cell mem_cell_64 (
    .\input (in_4[7]), .mode(in_3[0]), .select(A0111_out), .\output (mem_cell_64_output), .in_4(clk));
  or or_9 (or_9_out, mem_cell_33_output, mem_cell_41_output, or_1_out, mem_cell_49_output, mem_cell_57_output);
  or or_10 (or_10_out, mem_cell_34_output, mem_cell_42_output, or_2_out, mem_cell_50_output, mem_cell_58_output);
  or or_11 (or_11_out, mem_cell_35_output, mem_cell_43_output, or_3_out, mem_cell_51_output, mem_cell_59_output);
  or or_12 (or_12_out, mem_cell_36_output, mem_cell_44_output, or_4_out, mem_cell_52_output, mem_cell_60_output);
  or or_13 (or_13_out, mem_cell_37_output, mem_cell_45_output, or_5_out, mem_cell_53_output, mem_cell_61_output);
  or or_14 (or_14_out, mem_cell_38_output, mem_cell_46_output, or_6_out, mem_cell_54_output, mem_cell_62_output);
  or or_15 (or_15_out, mem_cell_39_output, mem_cell_47_output, or_7_out, mem_cell_55_output, mem_cell_63_output);
  or or_16 (or_16_out, mem_cell_40_output, mem_cell_48_output, or_8_out, mem_cell_56_output, mem_cell_64_output);
  and A1000 (A1000_out, in_2[3], not_1_out, not_3_out, not_2_out);
  mem_cell mem_cell_65 (
    .\input (in_4[0]), .mode(in_3[0]), .select(A1000_out), .\output (mem_cell_65_output), .in_4(clk));
  mem_cell mem_cell_66 (
    .\input (in_4[1]), .mode(in_3[0]), .select(A1000_out), .\output (mem_cell_66_output), .in_4(clk));
  mem_cell mem_cell_67 (
    .\input (in_4[2]), .mode(in_3[0]), .select(A1000_out), .\output (mem_cell_67_output), .in_4(clk));
  mem_cell mem_cell_68 (
    .\input (in_4[3]), .mode(in_3[0]), .select(A1000_out), .\output (mem_cell_68_output), .in_4(clk));
  mem_cell mem_cell_69 (
    .\input (in_4[4]), .mode(in_3[0]), .select(A1000_out), .\output (mem_cell_69_output), .in_4(clk));
  mem_cell mem_cell_70 (
    .\input (in_4[5]), .mode(in_3[0]), .select(A1000_out), .\output (mem_cell_70_output), .in_4(clk));
  mem_cell mem_cell_71 (
    .\input (in_4[6]), .mode(in_3[0]), .select(A1000_out), .\output (mem_cell_71_output), .in_4(clk));
  mem_cell mem_cell_72 (
    .\input (in_4[7]), .mode(in_3[0]), .select(A1000_out), .\output (mem_cell_72_output), .in_4(clk));
  and A1001 (A1001_out, in_2[3], not_1_out, not_3_out, in_2[0]);
  mem_cell mem_cell_73 (
    .\input (in_4[0]), .mode(in_3[0]), .select(A1001_out), .\output (mem_cell_73_output), .in_4(clk));
  mem_cell mem_cell_74 (
    .\input (in_4[1]), .mode(in_3[0]), .select(A1001_out), .\output (mem_cell_74_output), .in_4(clk));
  mem_cell mem_cell_75 (
    .\input (in_4[2]), .mode(in_3[0]), .select(A1001_out), .\output (mem_cell_75_output), .in_4(clk));
  mem_cell mem_cell_76 (
    .\input (in_4[3]), .mode(in_3[0]), .select(A1001_out), .\output (mem_cell_76_output), .in_4(clk));
  mem_cell mem_cell_77 (
    .\input (in_4[4]), .mode(in_3[0]), .select(A1001_out), .\output (mem_cell_77_output), .in_4(clk));
  mem_cell mem_cell_78 (
    .\input (in_4[5]), .mode(in_3[0]), .select(A1001_out), .\output (mem_cell_78_output), .in_4(clk));
  mem_cell mem_cell_79 (
    .\input (in_4[6]), .mode(in_3[0]), .select(A1001_out), .\output (mem_cell_79_output), .in_4(clk));
  mem_cell mem_cell_80 (
    .\input (in_4[7]), .mode(in_3[0]), .select(A1001_out), .\output (mem_cell_80_output), .in_4(clk));
  and A1010 (A1010_out, in_2[3], not_1_out, in_2[1], not_2_out);
  mem_cell mem_cell_81 (
    .\input (in_4[0]), .mode(in_3[0]), .select(A1010_out), .\output (mem_cell_81_output), .in_4(clk));
  mem_cell mem_cell_82 (
    .\input (in_4[1]), .mode(in_3[0]), .select(A1010_out), .\output (mem_cell_82_output), .in_4(clk));
  mem_cell mem_cell_83 (
    .\input (in_4[2]), .mode(in_3[0]), .select(A1010_out), .\output (mem_cell_83_output), .in_4(clk));
  mem_cell mem_cell_84 (
    .\input (in_4[3]), .mode(in_3[0]), .select(A1010_out), .\output (mem_cell_84_output), .in_4(clk));
  mem_cell mem_cell_85 (
    .\input (in_4[4]), .mode(in_3[0]), .select(A1010_out), .\output (mem_cell_85_output), .in_4(clk));
  mem_cell mem_cell_86 (
    .\input (in_4[5]), .mode(in_3[0]), .select(A1010_out), .\output (mem_cell_86_output), .in_4(clk));
  mem_cell mem_cell_87 (
    .\input (in_4[6]), .mode(in_3[0]), .select(A1010_out), .\output (mem_cell_87_output), .in_4(clk));
  mem_cell mem_cell_88 (
    .\input (in_4[7]), .mode(in_3[0]), .select(A1010_out), .\output (mem_cell_88_output), .in_4(clk));
  and A1011 (A1011_out, in_2[3], not_1_out, in_2[1], in_2[0]);
  mem_cell mem_cell_89 (
    .\input (in_4[0]), .mode(in_3[0]), .select(A1011_out), .\output (mem_cell_89_output), .in_4(clk));
  mem_cell mem_cell_90 (
    .\input (in_4[1]), .mode(in_3[0]), .select(A1011_out), .\output (mem_cell_90_output), .in_4(clk));
  mem_cell mem_cell_91 (
    .\input (in_4[2]), .mode(in_3[0]), .select(A1011_out), .\output (mem_cell_91_output), .in_4(clk));
  mem_cell mem_cell_92 (
    .\input (in_4[3]), .mode(in_3[0]), .select(A1011_out), .\output (mem_cell_92_output), .in_4(clk));
  mem_cell mem_cell_93 (
    .\input (in_4[4]), .mode(in_3[0]), .select(A1011_out), .\output (mem_cell_93_output), .in_4(clk));
  mem_cell mem_cell_94 (
    .\input (in_4[5]), .mode(in_3[0]), .select(A1011_out), .\output (mem_cell_94_output), .in_4(clk));
  mem_cell mem_cell_95 (
    .\input (in_4[6]), .mode(in_3[0]), .select(A1011_out), .\output (mem_cell_95_output), .in_4(clk));
  mem_cell mem_cell_96 (
    .\input (in_4[7]), .mode(in_3[0]), .select(A1011_out), .\output (mem_cell_96_output), .in_4(clk));
  and A1100 (A1100_out, in_2[3], in_2[2], not_3_out, not_2_out);
  or or_17 (or_17_out, mem_cell_65_output, mem_cell_73_output, or_9_out, mem_cell_81_output, mem_cell_89_output);
  or or_18 (or_18_out, mem_cell_66_output, mem_cell_74_output, or_10_out, mem_cell_82_output, mem_cell_90_output);
  or or_19 (or_19_out, mem_cell_67_output, mem_cell_75_output, or_11_out, mem_cell_83_output, mem_cell_91_output);
  or or_20 (or_20_out, mem_cell_68_output, mem_cell_76_output, or_12_out, mem_cell_84_output, mem_cell_92_output);
  or or_21 (or_21_out, mem_cell_69_output, mem_cell_77_output, or_13_out, mem_cell_85_output, mem_cell_93_output);
  or or_22 (or_22_out, mem_cell_70_output, mem_cell_78_output, or_14_out, mem_cell_86_output, mem_cell_94_output);
  or or_23 (or_23_out, mem_cell_71_output, mem_cell_79_output, or_15_out, mem_cell_87_output, mem_cell_95_output);
  or or_24 (or_24_out, mem_cell_72_output, mem_cell_80_output, or_16_out, mem_cell_88_output, mem_cell_96_output);
  mem_cell mem_cell_97 (
    .\input (in_4[0]), .mode(in_3[0]), .select(A1100_out), .\output (mem_cell_97_output), .in_4(clk));
  mem_cell mem_cell_98 (
    .\input (in_4[1]), .mode(in_3[0]), .select(A1100_out), .\output (mem_cell_98_output), .in_4(clk));
  mem_cell mem_cell_99 (
    .\input (in_4[2]), .mode(in_3[0]), .select(A1100_out), .\output (mem_cell_99_output), .in_4(clk));
  mem_cell mem_cell_100 (
    .\input (in_4[3]), .mode(in_3[0]), .select(A1100_out), .\output (mem_cell_100_output), .in_4(clk));
  mem_cell mem_cell_101 (
    .\input (in_4[4]), .mode(in_3[0]), .select(A1100_out), .\output (mem_cell_101_output), .in_4(clk));
  mem_cell mem_cell_102 (
    .\input (in_4[5]), .mode(in_3[0]), .select(A1100_out), .\output (mem_cell_102_output), .in_4(clk));
  mem_cell mem_cell_103 (
    .\input (in_4[6]), .mode(in_3[0]), .select(A1100_out), .\output (mem_cell_103_output), .in_4(clk));
  mem_cell mem_cell_104 (
    .\input (in_4[7]), .mode(in_3[0]), .select(A1100_out), .\output (mem_cell_104_output), .in_4(clk));
  and A1101 (A1101_out, in_2[3], in_2[2], not_3_out, in_2[0]);
  mem_cell mem_cell_105 (
    .\input (in_4[0]), .mode(in_3[0]), .select(A1101_out), .\output (mem_cell_105_output), .in_4(clk));
  mem_cell mem_cell_106 (
    .\input (in_4[1]), .mode(in_3[0]), .select(A1101_out), .\output (mem_cell_106_output), .in_4(clk));
  mem_cell mem_cell_107 (
    .\input (in_4[2]), .mode(in_3[0]), .select(A1101_out), .\output (mem_cell_107_output), .in_4(clk));
  mem_cell mem_cell_108 (
    .\input (in_4[3]), .mode(in_3[0]), .select(A1101_out), .\output (mem_cell_108_output), .in_4(clk));
  mem_cell mem_cell_109 (
    .\input (in_4[4]), .mode(in_3[0]), .select(A1101_out), .\output (mem_cell_109_output), .in_4(clk));
  mem_cell mem_cell_110 (
    .\input (in_4[5]), .mode(in_3[0]), .select(A1101_out), .\output (mem_cell_110_output), .in_4(clk));
  mem_cell mem_cell_111 (
    .\input (in_4[6]), .mode(in_3[0]), .select(A1101_out), .\output (mem_cell_111_output), .in_4(clk));
  mem_cell mem_cell_112 (
    .\input (in_4[7]), .mode(in_3[0]), .select(A1101_out), .\output (mem_cell_112_output), .in_4(clk));
  and A1110 (A1110_out, in_2[3], in_2[2], in_2[1], not_2_out);
  mem_cell mem_cell_113 (
    .\input (in_4[0]), .mode(in_3[0]), .select(A1110_out), .\output (mem_cell_113_output), .in_4(clk));
  mem_cell mem_cell_114 (
    .\input (in_4[1]), .mode(in_3[0]), .select(A1110_out), .\output (mem_cell_114_output), .in_4(clk));
  mem_cell mem_cell_115 (
    .\input (in_4[2]), .mode(in_3[0]), .select(A1110_out), .\output (mem_cell_115_output), .in_4(clk));
  mem_cell mem_cell_116 (
    .\input (in_4[3]), .mode(in_3[0]), .select(A1110_out), .\output (mem_cell_116_output), .in_4(clk));
  mem_cell mem_cell_117 (
    .\input (in_4[4]), .mode(in_3[0]), .select(A1110_out), .\output (mem_cell_117_output), .in_4(clk));
  mem_cell mem_cell_118 (
    .\input (in_4[5]), .mode(in_3[0]), .select(A1110_out), .\output (mem_cell_118_output), .in_4(clk));
  mem_cell mem_cell_119 (
    .\input (in_4[6]), .mode(in_3[0]), .select(A1110_out), .\output (mem_cell_119_output), .in_4(clk));
  mem_cell mem_cell_120 (
    .\input (in_4[7]), .mode(in_3[0]), .select(A1110_out), .\output (mem_cell_120_output), .in_4(clk));
  and A111 (A111_out, in_2[3], in_2[2], in_2[1], in_2[0]);
  mem_cell mem_cell_121 (
    .\input (in_4[0]), .mode(in_3[0]), .select(A111_out), .\output (mem_cell_121_output), .in_4(clk));
  mem_cell mem_cell_122 (
    .\input (in_4[1]), .mode(in_3[0]), .select(A111_out), .\output (mem_cell_122_output), .in_4(clk));
  mem_cell mem_cell_123 (
    .\input (in_4[2]), .mode(in_3[0]), .select(A111_out), .\output (mem_cell_123_output), .in_4(clk));
  mem_cell mem_cell_124 (
    .\input (in_4[3]), .mode(in_3[0]), .select(A111_out), .\output (mem_cell_124_output), .in_4(clk));
  mem_cell mem_cell_125 (
    .\input (in_4[4]), .mode(in_3[0]), .select(A111_out), .\output (mem_cell_125_output), .in_4(clk));
  mem_cell mem_cell_126 (
    .\input (in_4[5]), .mode(in_3[0]), .select(A111_out), .\output (mem_cell_126_output), .in_4(clk));
  mem_cell mem_cell_127 (
    .\input (in_4[6]), .mode(in_3[0]), .select(A111_out), .\output (mem_cell_127_output), .in_4(clk));
  mem_cell mem_cell_128 (
    .\input (in_4[7]), .mode(in_3[0]), .select(A111_out), .\output (mem_cell_128_output), .in_4(clk));
  or or_25 (data_output[0], mem_cell_97_output, mem_cell_105_output, or_17_out, mem_cell_113_output, mem_cell_121_output);
  or or_26 (data_output[1], mem_cell_98_output, mem_cell_106_output, or_18_out, mem_cell_114_output, mem_cell_122_output);
  or or_27 (data_output[2], mem_cell_99_output, mem_cell_107_output, or_19_out, mem_cell_115_output, mem_cell_123_output);
  or or_28 (data_output[3], mem_cell_100_output, mem_cell_108_output, or_20_out, mem_cell_116_output, mem_cell_124_output);
  or or_29 (data_output[4], mem_cell_101_output, mem_cell_109_output, or_21_out, mem_cell_117_output, mem_cell_125_output);
  or or_30 (data_output[5], mem_cell_102_output, mem_cell_110_output, or_22_out, mem_cell_118_output, mem_cell_126_output);
  or or_31 (data_output[6], mem_cell_103_output, mem_cell_111_output, or_23_out, mem_cell_119_output, mem_cell_127_output);
  or or_32 (data_output[7], mem_cell_104_output, mem_cell_112_output, or_24_out, mem_cell_120_output, mem_cell_128_output);

  // Notes on the sheet:
  //   address input
  //   data input
  //   address space
  //   mode input 
  //   data space
  //   RAM
endmodule

module MODE_REG (
  input  I,
  input  in_2,
  output [7:0] O
);

  wire not_1_out;

  J_K_Flip_Flop j_k_ff_1 (.J(I), .K(not_1_out), .clk(in_2), .Q(O[0]));  // open: Qn, preset, reset
  not not_1 (not_1_out, I);

  assign O[7:1] = {7{1'b0}};
endmodule

module GENERAL_REG (
  input  [7:0] I,
  input  in_2,
  output [7:0] O
);

  D_Flip_Flop d_ff_1 (.D(I[0]), .clk(in_2), .Q(O[0]));  // open: Qn, preset, reset
  D_Flip_Flop d_ff_2 (.D(I[1]), .clk(in_2), .Q(O[1]));  // open: Qn, preset, reset
  D_Flip_Flop d_ff_3 (.D(I[2]), .clk(in_2), .Q(O[2]));  // open: Qn, preset, reset
  D_Flip_Flop d_ff_4 (.D(I[3]), .clk(in_2), .Q(O[3]));  // open: Qn, preset, reset
  D_Flip_Flop d_ff_5 (.D(I[4]), .clk(in_2), .Q(O[4]));  // open: Qn, preset, reset
  D_Flip_Flop d_ff_6 (.D(I[5]), .clk(in_2), .Q(O[5]));  // open: Qn, preset, reset
  D_Flip_Flop d_ff_7 (.D(I[6]), .clk(in_2), .Q(O[6]));  // open: Qn, preset, reset
  D_Flip_Flop d_ff_8 (.D(I[7]), .clk(in_2), .Q(O[7]));  // open: Qn, preset, reset
endmodule

module INCBY1 (
  input  [7:0] from_PC,
  output [7:0] to_PC
);

  wire and_1_out, and_2_out, and_3_out, and_4_out, and_5_out, and_6_out, and_7_out;

  xor xor_1 (to_PC[0], from_PC[0], 1'b1);
  and and_1 (and_1_out, from_PC[0], 1'b1);
  xor xor_2 (to_PC[1], and_1_out, from_PC[1]);
  and and_2 (and_2_out, and_1_out, from_PC[1]);
  xor xor_3 (to_PC[2], and_2_out, from_PC[2]);
  and and_3 (and_3_out, and_2_out, from_PC[2]);
  xor xor_4 (to_PC[3], and_3_out, from_PC[3]);
  and and_4 (and_4_out, and_3_out, from_PC[3]);
  xor xor_5 (to_PC[4], and_4_out, from_PC[4]);
  and and_5 (and_5_out, and_4_out, from_PC[4]);
  xor xor_6 (to_PC[5], and_5_out, from_PC[5]);
  and and_6 (and_6_out, and_5_out, from_PC[5]);
  xor xor_7 (to_PC[6], and_6_out, from_PC[6]);
  and and_7 (and_7_out, and_6_out, from_PC[6]);
  xor xor_8 (to_PC[7], and_7_out, from_PC[7]);
  // AND_Gate and_8 has open pins: in0=and_7_out, in1=from_PC[7], out=open
endmodule

module add1bit (
  input  in_1,
  input  in_2,
  input  in_3,
  output out_4,
  output out_5
);

  wire and_1_out, and_2_out, xor_1_out;

  xor xor_1 (xor_1_out, in_2, in_3);
  and and_1 (and_1_out, in_1, xor_1_out);
  and and_2 (and_2_out, in_2, in_3);
  xor xor_2 (out_4, in_1, xor_1_out);
  or or_1 (out_5, and_1_out, and_2_out);
endmodule

module ALU (
  input  Mode,
  input  [7:0] L,
  input  ALU_ACTV,
  input  L_W,
  input  [7:0] R,
  input  R_W,
  output [7:0] O,
  output [7:0] Flags
);

  wire and_1_out, full_adder_1_out_5, full_adder_2_out_5, full_adder_3_out_5, full_adder_4_out_5,
       full_adder_5_out_5, full_adder_6_out_5, full_adder_7_out_5, not_1_out, not_2_out, not_3_out,
       not_4_out, not_6_out, not_7_out, not_8_out, not_9_out;
  wire [2:0] and_3_out;
  wire [7:0] LEFT_REGISTER_o, RIGHT_REGISTER_o, twos_comp_converter_1_out_3, xor_1_out;

  // Probe on L
  // Probe on R
  TWOS_COMP_CONVERTER twos_comp_converter_1 (.out_3(twos_comp_converter_1_out_3), .in_2(LEFT_REGISTER_o), .in_1(Mode));
  GENERAL_REG LEFT_REGISTER (.O(LEFT_REGISTER_o), .in_2(L_W));  // open: I
  GENERAL_REG RIGHT_REGISTER (.O(RIGHT_REGISTER_o), .in_2(R_W));  // open: I
  xor xor_1 (xor_1_out[0], twos_comp_converter_1_out_3[0], RIGHT_REGISTER_o[0]);
  and and_1 (and_1_out, twos_comp_converter_1_out_3[0], RIGHT_REGISTER_o[0]);
  FULL_ADDER full_adder_1 (
    .out_5(full_adder_1_out_5), .Carry_In(RIGHT_REGISTER_o[1]), .Sum(xor_1_out[1]), .A(and_1_out),
    .B(twos_comp_converter_1_out_3[1]));
  FULL_ADDER full_adder_2 (
    .out_5(full_adder_2_out_5), .Carry_In(RIGHT_REGISTER_o[2]), .Sum(xor_1_out[2]), .A(full_adder_1_out_5),
    .B(twos_comp_converter_1_out_3[2]));
  FULL_ADDER full_adder_3 (
    .out_5(full_adder_3_out_5), .Carry_In(RIGHT_REGISTER_o[3]), .Sum(xor_1_out[3]), .A(full_adder_2_out_5),
    .B(twos_comp_converter_1_out_3[3]));
  FULL_ADDER full_adder_4 (
    .out_5(full_adder_4_out_5), .Carry_In(RIGHT_REGISTER_o[4]), .Sum(xor_1_out[4]), .A(full_adder_3_out_5),
    .B(twos_comp_converter_1_out_3[4]));
  FULL_ADDER full_adder_5 (
    .out_5(full_adder_5_out_5), .Carry_In(RIGHT_REGISTER_o[5]), .Sum(xor_1_out[5]), .A(full_adder_4_out_5),
    .B(twos_comp_converter_1_out_3[5]));
  FULL_ADDER full_adder_6 (
    .out_5(full_adder_6_out_5), .Carry_In(RIGHT_REGISTER_o[6]), .Sum(xor_1_out[6]), .A(full_adder_5_out_5),
    .B(twos_comp_converter_1_out_3[6]));
  FULL_ADDER full_adder_7 (
    .out_5(full_adder_7_out_5), .Carry_In(RIGHT_REGISTER_o[7]), .Sum(xor_1_out[7]), .A(full_adder_6_out_5),
    .B(twos_comp_converter_1_out_3[7]));
  not not_1 (not_1_out, Mode);
  and and_2 (and_3_out[2], not_1_out, full_adder_7_out_5);
  not not_2 (not_2_out, xor_1_out[0]);
  not not_3 (not_3_out, xor_1_out[1]);
  not not_4 (not_4_out, xor_1_out[2]);
  not not_5 (not_4_out, xor_1_out[3]);
  and and_3 (and_3_out[0], not_2_out, not_3_out, not_4_out, not_4_out, not_6_out, not_7_out, not_8_out, not_9_out);
  not not_6 (not_6_out, xor_1_out[4]);
  not not_7 (not_7_out, xor_1_out[5]);
  not not_8 (not_8_out, xor_1_out[6]);
  not not_9 (not_9_out, xor_1_out[7]);
  and and_4 (and_3_out[1], Mode, xor_1_out[7]);
  GENERAL_REG A_REGISTER (.I(xor_1_out), .O(O), .in_2(ALU_ACTV));
  GENERAL_REG general_reg_1 (.I({{5{1'b0}}, and_3_out}), .O(Flags), .in_2(ALU_ACTV));
  // Probe on O

  // Notes on the sheet:
  //   Clock
  //   010 = NEGATIVE
  //   001 = ZERO
  //   100 = OVERFLOW
endmodule

module FULL_ADDER (
  input  A,
  input  B,
  input  Carry_In,
  output Sum,
  output out_5
);

  wire and_1_out, and_2_out, xor_1_out;

  xor xor_1 (xor_1_out, A, B);
  xor xor_2 (Sum, xor_1_out, Carry_In);
  and and_1 (and_1_out, xor_1_out, Carry_In);
  and and_2 (and_2_out, A, B);
  or or_1 (out_5, and_1_out, and_2_out);

  // Notes on the sheet:
  //   Carry_Out
endmodule

module TWOS_COMP_CONVERTER (
  input  in_1,
  input  [7:0] in_2,
  output [7:0] out_3
);

  wire and_1_out, and_2_out, and_3_out, and_4_out, and_5_out, and_6_out, and_7_out, xor_1_out, xor_2_out,
       xor_3_out, xor_4_out, xor_5_out, xor_6_out, xor_7_out, xor_8_out;

  xor xor_1 (xor_1_out, in_2[0], in_1);
  xor xor_2 (xor_2_out, in_2[1], in_1);
  xor xor_3 (xor_3_out, in_2[2], in_1);
  xor xor_4 (xor_4_out, in_2[3], in_1);
  xor xor_5 (xor_5_out, in_2[4], in_1);
  xor xor_6 (xor_6_out, in_2[5], in_1);
  xor xor_7 (xor_7_out, in_2[6], in_1);
  xor xor_8 (xor_8_out, in_2[7], in_1);
  xor xor_9 (out_3[0], xor_1_out, in_1);
  and and_1 (and_1_out, xor_1_out, in_1);
  and and_2 (and_2_out, and_1_out, xor_2_out);
  xor xor_10 (out_3[1], and_1_out, xor_2_out);
  xor xor_11 (out_3[2], and_2_out, xor_3_out);
  and and_3 (and_3_out, and_2_out, xor_3_out);
  xor xor_12 (out_3[3], and_3_out, xor_4_out);
  and and_4 (and_4_out, and_3_out, xor_4_out);
  and and_5 (and_5_out, and_4_out, xor_5_out);
  xor xor_13 (out_3[4], and_4_out, xor_5_out);
  xor xor_14 (out_3[5], and_5_out, xor_6_out);
  and and_6 (and_6_out, and_5_out, xor_6_out);
  xor xor_15 (out_3[6], and_6_out, xor_7_out);
  and and_7 (and_7_out, and_6_out, xor_7_out);
  xor xor_16 (out_3[7], and_7_out, xor_8_out);
endmodule

module INPUT_BUFFER (
  input  in_1,
  input  in_2,
  input  in_3,
  input  in_4,
  input  in_5,
  input  in_6,
  input  in_7,
  input  in_8,
  input  in_9,
  input  in_10,
  output [7:0] out_11
);

  Priority_Encoder #(.select(4)) priority_encoder_1 (
    .in0(in_1), .in1(in_2), .in2(in_3), .in3(in_4), .in4(in_5), .in5(in_6), .in6(in_7), .in7(in_8),
    .in8(in_9), .in9(in_10), .in10(1'b0), .in11(1'b0), .in12(1'b0), .in13(1'b0), .in14(1'b0), .in15(1'b0),
    .out(out_11[3:0]));  // open: gs, en_out, en_in

  assign out_11[7:4] = 4'b0000;
endmodule

module DISP_HELP_THREE_SHIFT (
  input  in_1,
  input  in_2,
  input  in_3,
  input  in_4,
  output out_5,
  output out_6,
  output out_7,
  output out_8
);

  wire adder_1_cout, adder_2_cout, adder_3_cout, and_1_out, and_2_out, or_1_out;

  and and_1 (and_1_out, in_1, in_3);
  and and_2 (and_2_out, in_2, in_3);
  or or_1 (or_1_out, and_1_out, and_2_out, in_4);
  Adder #(.width(1)) adder_1 (.a(in_1), .b(or_1_out), .out(out_5), .cout(adder_1_cout));  // open: cin
  Adder #(.width(1)) adder_2 (.a(adder_1_cout), .b(in_2), .out(out_6), .cin(or_1_out), .cout(adder_2_cout));
  Adder #(.width(1)) adder_3 (.a(adder_2_cout), .b(in_3), .out(out_7), .cout(adder_3_cout));  // open: cin
  Adder #(.width(1)) adder_4 (.a(adder_3_cout), .b(in_4), .out(out_8));  // open: cin, cout
endmodule

module DISPLAY (
  input  [7:0] in_1,
  output [6:0] out_2,
  output [6:0] out_3,
  output [6:0] out_4
);

  wire decoder_1_out0, decoder_1_out1, decoder_1_out2, decoder_1_out3, decoder_1_out4, decoder_1_out5,
       decoder_1_out6, decoder_1_out7, decoder_1_out8, decoder_1_out9, decoder_1_out10, decoder_1_out11,
       decoder_1_out12, decoder_1_out13, decoder_1_out14, decoder_1_out15, decoder_2_out0, decoder_2_out1,
       decoder_2_out2, decoder_2_out3, decoder_2_out4, decoder_2_out5, decoder_2_out6, decoder_2_out7,
       decoder_2_out8, decoder_2_out9, decoder_2_out10, decoder_2_out11, decoder_2_out12, decoder_2_out13,
       decoder_2_out14, decoder_2_out15, decoder_3_out0, decoder_3_out1, decoder_3_out2, decoder_3_out3,
       decoder_3_out4, decoder_3_out5, decoder_3_out6, decoder_3_out7, decoder_3_out8, decoder_3_out9,
       decoder_3_out10, decoder_3_out11, decoder_3_out12, decoder_3_out13, decoder_3_out14, decoder_3_out15,
       disp_help_three_shift_1_out_5, disp_help_three_shift_1_out_6, disp_help_three_shift_1_out_7,
       disp_help_three_shift_1_out_8, disp_help_three_shift_2_out_5, disp_help_three_shift_2_out_6,
       disp_help_three_shift_2_out_7, disp_help_three_shift_2_out_8, disp_help_three_shift_3_out_5,
       disp_help_three_shift_3_out_6, disp_help_three_shift_3_out_7, disp_help_three_shift_3_out_8,
       disp_help_three_shift_4_out_5, disp_help_three_shift_4_out_6, disp_help_three_shift_4_out_7,
       disp_help_three_shift_5_out_5, disp_help_three_shift_5_out_6, disp_help_three_shift_5_out_7,
       disp_help_three_shift_5_out_8, not_1_out, not_2_out, not_3_out, not_4_out, not_5_out, not_6_out,
       not_7_out, not_8_out, not_10_out, not_11_out, not_12_out, not_13_out, not_14_out, not_15_out,
       not_16_out, not_17_out, not_18_out, not_19_out, not_20_out, not_22_out, not_23_out, not_24_out,
       not_25_out, not_26_out, not_27_out, not_28_out, not_29_out, not_30_out, not_31_out, not_32_out,
       not_33_out, not_34_out, not_35_out, not_36_out, not_37_out, not_38_out, not_39_out, not_40_out,
       not_41_out, not_42_out, not_43_out, not_44_out, not_45_out, not_46_out, not_47_out;
  wire [1:0] disp_help_three_shift_6_out_8;
  wire [3:0] disp_help_three_shift_7_out_8;
  wire [3:1] disp_help_three_shift_7_out_5;

  DISP_HELP_THREE_SHIFT disp_help_three_shift_1 (
    .in_1(in_1[5]), .out_5(disp_help_three_shift_1_out_5), .in_2(in_1[6]),
    .out_6(disp_help_three_shift_1_out_6), .out_7(disp_help_three_shift_1_out_7), .in_3(in_1[7]),
    .out_8(disp_help_three_shift_1_out_8), .in_4(1'b0));
  DISP_HELP_THREE_SHIFT disp_help_three_shift_2 (
    .in_1(in_1[4]), .out_5(disp_help_three_shift_2_out_5), .in_2(disp_help_three_shift_1_out_5),
    .out_6(disp_help_three_shift_2_out_6), .out_7(disp_help_three_shift_2_out_7),
    .in_3(disp_help_three_shift_1_out_6), .out_8(disp_help_three_shift_2_out_8),
    .in_4(disp_help_three_shift_1_out_7));
  DISP_HELP_THREE_SHIFT disp_help_three_shift_3 (
    .in_1(in_1[3]), .out_5(disp_help_three_shift_3_out_5), .in_2(disp_help_three_shift_2_out_5),
    .out_6(disp_help_three_shift_3_out_6), .out_7(disp_help_three_shift_3_out_7),
    .in_3(disp_help_three_shift_2_out_6), .out_8(disp_help_three_shift_3_out_8),
    .in_4(disp_help_three_shift_2_out_7));
  DISP_HELP_THREE_SHIFT disp_help_three_shift_4 (
    .in_1(disp_help_three_shift_3_out_8), .out_5(disp_help_three_shift_4_out_5),
    .in_2(disp_help_three_shift_2_out_8), .out_6(disp_help_three_shift_4_out_6),
    .out_7(disp_help_three_shift_4_out_7), .in_3(disp_help_three_shift_1_out_8),
    .out_8(disp_help_three_shift_6_out_8[1]), .in_4(1'b0));
  DISP_HELP_THREE_SHIFT disp_help_three_shift_5 (
    .in_1(in_1[2]), .out_5(disp_help_three_shift_5_out_5), .in_2(disp_help_three_shift_3_out_5),
    .out_6(disp_help_three_shift_5_out_6), .out_7(disp_help_three_shift_5_out_7),
    .in_3(disp_help_three_shift_3_out_6), .out_8(disp_help_three_shift_5_out_8),
    .in_4(disp_help_three_shift_3_out_7));
  DISP_HELP_THREE_SHIFT disp_help_three_shift_6 (
    .in_1(disp_help_three_shift_5_out_8), .out_5(disp_help_three_shift_7_out_8[1]),
    .in_2(disp_help_three_shift_4_out_5), .out_6(disp_help_three_shift_7_out_8[2]),
    .out_7(disp_help_three_shift_7_out_8[3]), .in_3(disp_help_three_shift_4_out_6),
    .out_8(disp_help_three_shift_6_out_8[0]), .in_4(disp_help_three_shift_4_out_7));
  DISP_HELP_THREE_SHIFT disp_help_three_shift_7 (
    .in_1(in_1[1]), .out_5(disp_help_three_shift_7_out_5[1]), .in_2(disp_help_three_shift_5_out_5),
    .out_6(disp_help_three_shift_7_out_5[2]), .out_7(disp_help_three_shift_7_out_5[3]),
    .in_3(disp_help_three_shift_5_out_6), .out_8(disp_help_three_shift_7_out_8[0]),
    .in_4(disp_help_three_shift_5_out_7));
  Decoder #(.select(4), .enable("false")) decoder_1 (
    .out0(decoder_1_out0), .out1(decoder_1_out1), .out2(decoder_1_out2), .out3(decoder_1_out3),
    .out4(decoder_1_out4), .out5(decoder_1_out5), .out6(decoder_1_out6), .out7(decoder_1_out7),
    .out8(decoder_1_out8), .out9(decoder_1_out9), .out10(decoder_1_out10), .out11(decoder_1_out11),
    .out12(decoder_1_out12), .out13(decoder_1_out13), .out14(decoder_1_out14), .out15(decoder_1_out15),
    .sel({disp_help_three_shift_7_out_5, in_1[0]}));
  not not_1 (not_1_out, decoder_1_out1);
  not not_2 (not_2_out, decoder_1_out4);
  not not_3 (not_3_out, decoder_1_out9);
  not not_4 (not_4_out, decoder_1_out7);
  not not_5 (not_5_out, decoder_1_out1);
  and and_1 (out_4[0], not_5_out, not_6_out);
  not not_6 (not_6_out, decoder_1_out4);
  not not_7 (not_7_out, decoder_1_out5);
  and and_2 (out_4[1], not_7_out, not_8_out);
  not not_8 (not_8_out, decoder_1_out6);
  not not_9 (out_4[2], decoder_1_out2);
  and and_3 (out_4[3], not_1_out, not_2_out, not_3_out, not_4_out);
  or or_1 (out_4[4], decoder_1_out2, decoder_1_out0, decoder_1_out6, decoder_1_out8);
  not not_10 (not_10_out, decoder_1_out1);
  not not_11 (not_11_out, decoder_1_out2);
  and and_4 (out_4[5], not_10_out, not_11_out, not_12_out, not_13_out);
  not not_12 (not_12_out, decoder_1_out7);
  not not_13 (not_13_out, decoder_1_out3);
  not not_14 (not_14_out, decoder_1_out0);
  and and_5 (out_4[6], not_14_out, not_15_out, not_16_out);
  not not_15 (not_15_out, decoder_1_out1);
  not not_16 (not_16_out, decoder_1_out7);
  Decoder #(.select(4), .enable("false")) decoder_2 (
    .out0(decoder_2_out0), .out1(decoder_2_out1), .out2(decoder_2_out2), .out3(decoder_2_out3),
    .out4(decoder_2_out4), .out5(decoder_2_out5), .out6(decoder_2_out6), .out7(decoder_2_out7),
    .out8(decoder_2_out8), .out9(decoder_2_out9), .out10(decoder_2_out10), .out11(decoder_2_out11),
    .out12(decoder_2_out12), .out13(decoder_2_out13), .out14(decoder_2_out14), .out15(decoder_2_out15),
    .sel(disp_help_three_shift_7_out_8));
  not not_17 (not_17_out, decoder_2_out1);
  and and_6 (out_3[0], not_17_out, not_18_out);
  not not_18 (not_18_out, decoder_2_out4);
  not not_19 (not_19_out, decoder_2_out5);
  and and_7 (out_3[1], not_19_out, not_20_out);
  not not_20 (not_20_out, decoder_2_out6);
  not not_21 (out_3[2], decoder_2_out2);
  not not_22 (not_22_out, decoder_2_out1);
  not not_23 (not_23_out, decoder_2_out4);
  and and_8 (out_3[3], not_22_out, not_23_out, not_24_out, not_25_out);
  not not_24 (not_24_out, decoder_2_out9);
  not not_25 (not_25_out, decoder_2_out7);
  or or_2 (out_3[4], decoder_2_out2, decoder_2_out0, decoder_2_out6, decoder_2_out8);
  not not_26 (not_26_out, decoder_2_out1);
  not not_27 (not_27_out, decoder_2_out2);
  and and_9 (out_3[5], not_26_out, not_27_out, not_28_out, not_29_out);
  not not_28 (not_28_out, decoder_2_out7);
  not not_29 (not_29_out, decoder_2_out3);
  not not_30 (not_30_out, decoder_2_out0);
  not not_31 (not_31_out, decoder_2_out1);
  and and_10 (out_3[6], not_30_out, not_31_out, not_32_out);
  not not_32 (not_32_out, decoder_2_out7);
  Decoder #(.select(4), .enable("false")) decoder_3 (
    .out0(decoder_3_out0), .out1(decoder_3_out1), .out2(decoder_3_out2), .out3(decoder_3_out3),
    .out4(decoder_3_out4), .out5(decoder_3_out5), .out6(decoder_3_out6), .out7(decoder_3_out7),
    .out8(decoder_3_out8), .out9(decoder_3_out9), .out10(decoder_3_out10), .out11(decoder_3_out11),
    .out12(decoder_3_out12), .out13(decoder_3_out13), .out14(decoder_3_out14), .out15(decoder_3_out15),
    .sel({2'b00, disp_help_three_shift_6_out_8}));
  not not_33 (not_33_out, decoder_3_out1);
  and top_bar (out_2[0], not_33_out, not_34_out);
  not not_34 (not_34_out, decoder_3_out4);
  not not_35 (not_35_out, decoder_3_out5);
  and top_right (out_2[1], not_35_out, not_36_out);
  not not_36 (not_36_out, decoder_3_out6);
  not bottom_right (out_2[2], decoder_3_out2);
  not not_37 (not_37_out, decoder_3_out1);
  not not_38 (not_38_out, decoder_3_out4);
  and bottom_bar (out_2[3], not_37_out, not_38_out, not_39_out, not_40_out);
  not not_39 (not_39_out, decoder_3_out9);
  not not_40 (not_40_out, decoder_3_out7);
  or bottom_left (out_2[4], decoder_3_out2, decoder_3_out0, decoder_3_out6, decoder_3_out8);
  not not_41 (not_41_out, decoder_3_out1);
  not not_42 (not_42_out, decoder_3_out2);
  and top_left (out_2[5], not_41_out, not_42_out, not_43_out, not_44_out);
  not not_43 (not_43_out, decoder_3_out7);
  not not_44 (not_44_out, decoder_3_out3);
  not not_45 (not_45_out, decoder_3_out0);
  and middle_bar (out_2[6], not_45_out, not_46_out, not_47_out);
  not not_46 (not_46_out, decoder_3_out1);
  not not_47 (not_47_out, decoder_3_out7);
endmodule

module PROG_ROM (
);

  wire and_2_out, or_1_out;

  // AND_Gate and_1 is placed but not wired
  // AND_Gate and_2 has open pins: out=and_2_out
  // AND_Gate and_3 is placed but not wired
  // AND_Gate and_4 is placed but not wired
  // AND_Gate and_5 is placed but not wired
  // AND_Gate and_6 is placed but not wired
  // AND_Gate and_7 is placed but not wired
  // AND_Gate and_8 is placed but not wired
  // AND_Gate and_9 is placed but not wired
  // AND_Gate and_10 is placed but not wired
  // AND_Gate and_11 is placed but not wired
  // AND_Gate and_12 is placed but not wired
  // AND_Gate and_13 is placed but not wired
  // AND_Gate and_14 is placed but not wired
  // AND_Gate and_15 is placed but not wired
  // AND_Gate and_16 is placed but not wired
  // OR_Gate or_1 has open pins: out=or_1_out
  // OR_Gate or_2 is placed but not wired
  // OR_Gate or_3 is placed but not wired
  // OR_Gate or_4 is placed but not wired
  // OR_Gate or_5 is placed but not wired
  // OR_Gate or_6 has open pins: in0=and_2_out, in1=or_1_out, out=open
  // OR_Gate or_7 is placed but not wired
  // OR_Gate or_8 is placed but not wired
  // OR_Gate or_9 is placed but not wired
  // OR_Gate or_10 is placed but not wired
  // OR_Gate or_11 is placed but not wired
  // OR_Gate or_12 is placed but not wired
  // OR_Gate or_13 is placed but not wired
  // OR_Gate or_14 is placed but not wired
  // OR_Gate or_15 is placed but not wired
  // OR_Gate or_16 is placed but not wired
  // OR_Gate or_17 is placed but not wired
  // OR_Gate or_18 is placed but not wired
  // OR_Gate or_19 is placed but not wired
  // OR_Gate or_20 is placed but not wired
  // OR_Gate or_21 is placed but not wired
  // OR_Gate or_22 is placed but not wired
  // OR_Gate or_23 is placed but not wired
  // OR_Gate or_24 is placed but not wired
  // OR_Gate or_25 is placed but not wired
  // OR_Gate or_26 is placed but not wired
  // OR_Gate or_27 is placed but not wired
  // OR_Gate or_28 is placed but not wired
  // OR_Gate or_29 is placed but not wired
  // OR_Gate or_30 is placed but not wired
  // OR_Gate or_31 is placed but not wired
  // OR_Gate or_32 is placed but not wired
  // OR_Gate or_33 is placed but not wired
  // OR_Gate or_34 is placed but not wired
  // OR_Gate or_35 is placed but not wired
  // OR_Gate or_36 is placed but not wired
  // OR_Gate or_37 is placed but not wired
  // OR_Gate or_38 is placed but not wired
  // OR_Gate or_39 is placed but not wired
  // OR_Gate or_40 is placed but not wired
endmodule
