// Logisim project CU.circ as structural Verilog
module OP_ROM (
  input  [7:0] IRin,
  input  ACTV,
  output ADD,
  output SUB,
  output MULT,
  output LD,
  output SAV,
  output BEQ,
  output BNQ,
  output PRT,
  output INP,
  output STOP,
  output FLSH
);

  wire and_1_out, and_3_out, and_5_out, and_7_out, and_9_out, and_11_out, and_13_out, and_15_out, and_17_out,
       and_19_out, and_21_out, not_1_out, not_2_out, not_3_out, not_4_out, not_5_out, not_6_out, not_7_out,
       not_8_out, not_9_out, not_10_out, not_11_out, not_12_out, not_13_out, not_14_out, not_15_out,
       not_16_out, not_17_out, not_18_out, not_19_out, not_20_out, not_21_out, not_22_out, not_23_out,
       not_24_out, not_25_out, not_26_out, not_27_out, not_28_out, not_29_out, not_30_out, not_31_out,
       or_1_out;

  not not_1 (not_1_out, IRin[3]);
  not not_2 (not_2_out, IRin[4]);
  not not_3 (not_3_out, IRin[5]);
  not not_4 (not_4_out, IRin[4]);
  not not_5 (not_5_out, IRin[5]);
  not not_6 (not_6_out, IRin[5]);
  not not_7 (not_7_out, IRin[6]);
  not not_8 (not_8_out, IRin[6]);
  or or_1 (or_1_out, IRin[4], IRin[5]);
  not not_9 (not_9_out, IRin[6]);
  not not_10 (not_10_out, IRin[7]);
  not not_11 (not_11_out, IRin[7]);
  not not_12 (not_12_out, IRin[2]);
  not not_13 (not_13_out, IRin[3]);
  not not_14 (not_14_out, IRin[5]);
  not not_15 (not_15_out, IRin[3]);
  not not_16 (not_16_out, IRin[5]);
  not not_17 (not_17_out, IRin[1]);
  not not_18 (not_18_out, IRin[2]);
  not not_19 (not_19_out, IRin[3]);
  not not_20 (not_20_out, IRin[4]);
  not not_21 (not_21_out, IRin[5]);
  not not_22 (not_22_out, IRin[6]);
  not not_23 (not_23_out, IRin[7]);
  not not_24 (not_24_out, IRin[0]);
  not not_25 (not_25_out, IRin[1]);
  not not_26 (not_26_out, IRin[2]);
  not not_27 (not_27_out, IRin[3]);
  not not_28 (not_28_out, IRin[4]);
  not not_29 (not_29_out, IRin[5]);
  not not_30 (not_30_out, IRin[6]);
  not not_31 (not_31_out, IRin[7]);
  and and_1 (and_1_out, not_1_out, not_2_out, not_3_out, IRin[6], IRin[7]);
  and and_2 (ADD, and_1_out, ACTV);
  and and_3 (and_3_out, IRin[3], not_4_out, not_5_out, IRin[6], IRin[7]);
  and and_4 (SUB, and_3_out, ACTV);
  and and_5 (and_5_out, IRin[5], IRin[6], IRin[7]);
  and and_6 (MULT, and_5_out, ACTV);
  and and_7 (and_7_out, not_6_out, not_7_out, IRin[7]);
  and and_8 (LD, and_7_out, ACTV);
  and and_9 (and_9_out, IRin[5], not_8_out, IRin[7]);
  and and_10 (SAV, and_9_out, ACTV);
  and and_11 (and_11_out, or_1_out, not_9_out, not_10_out);
  and and_12 (BEQ, and_11_out, ACTV);
  and and_13 (and_13_out, IRin[6], not_11_out);
  and and_14 (BNQ, and_13_out, ACTV);
  and and_15 (and_15_out, not_12_out, not_13_out, IRin[4], not_14_out, IRin[6], IRin[7]);
  and and_16 (PRT, and_15_out, ACTV);
  and and_17 (and_17_out, IRin[2], not_15_out, IRin[4], not_16_out, IRin[6], IRin[7]);
  and and_18 (INP, and_17_out, ACTV);
  and and_19 (and_19_out, IRin[0], not_17_out, not_18_out, not_19_out, not_20_out, not_21_out, not_22_out, not_23_out);
  and and_20 (STOP, and_19_out, ACTV);
  and and_21 (and_21_out, not_24_out, not_25_out, not_26_out, not_27_out, not_28_out, not_29_out, not_30_out, not_31_out);
  and and_22 (FLSH, and_21_out, ACTV);
endmodule

module CU (
  input  [7:0] IRin,
  input  in_2,
  output Reg0,
  output Reg1,
  output R_W,
  output ALU_L,
  output ALU_R,
  output ALU_O,
  output ALU_EXE,
  output ALU_FLAG,
  output STAT,
  output MAR_IN,
  output MAR_OUT,
  output MBR_IN,
  output MBR_OUT,
  output IR,
  output PC_INC,
  output PC_A_I,
  output [3:0] PC_A_O,
  output PC_OUT,
  output BRANCH_SIGN,
  output DR_OUT,
  output DR_IN,
  output AR_IN,
  output RAM_R,
  output RAM_W,
  output [3:0] RAM_A,
  output PNT,
  output INPT
);

  wire add_sub_1_alu_exe, add_sub_1_alu_l, add_sub_1_alu_o, add_sub_1_alu_r, add_sub_1_done, add_sub_1_r0,
       add_sub_1_r1, add_sub_1_r_w, bnq_beq_1_alu_l, bnq_beq_1_alu_r, bnq_beq_1_alue_exe, bnq_beq_1_done,
       bnq_beq_1_pc_a_i, bnq_beq_1_r0, bnq_beq_1_r1, bnq_beq_1_stat, buffer_1_out, fetch_1_ar, fetch_1_done,
       fetch_1_dr_o, fetch_1_ir, fetch_1_mar_i, fetch_1_mar_o, fetch_1_mbr_i, fetch_1_mbr_o, fetch_1_pc_inc,
       fetch_1_pc_o, fetch_1_ram_r, inp_1_done, inp_1_inpt, inp_1_mbr_i, inp_1_mbr_o, inp_1_r0_i, inp_1_r1_i,
       ld_1_ar_i, ld_1_done, ld_1_dr_o, ld_1_mar_i, ld_1_mar_o, ld_1_mbr_i, ld_1_mbr_o, ld_1_r0_i, ld_1_r1_i,
       ld_1_ram_r, op_rom_1_add, op_rom_1_beq, op_rom_1_bnq, op_rom_1_inp, op_rom_1_ld, op_rom_1_prt,
       op_rom_1_sav, op_rom_1_sub, or_1_out, or_2_out, or_3_out, prt_1_disp, prt_1_done, prt_1_mbr_i,
       prt_1_mbr_o, prt_1_r0_o, prt_1_r1_o, sav_1_ar_in, sav_1_done, sav_1_dr_in, sav_1_mar_in,
       sav_1_mar_out, sav_1_mbr_in, sav_1_mbr_out, sav_1_r0_out, sav_1_r1_out, sav_1_ram_w, t_ff_1_q,
       t_ff_1_qn;
  wire [3:0] bnq_beq_1_pc_a_o, ld_1_ram_a, sav_1_ram_a;

  OP_ROM op_rom_1 (
    .IRin(IRin), .LD(op_rom_1_ld), .BEQ(op_rom_1_beq), .ADD(op_rom_1_add), .SAV(op_rom_1_sav),
    .SUB(op_rom_1_sub), .PRT(op_rom_1_prt), .INP(op_rom_1_inp), .BNQ(op_rom_1_bnq), .ACTV(t_ff_1_q));  // open: STOP, MULT, FLSH
  or or_1 (or_1_out, op_rom_1_add, op_rom_1_sub);
  Clock clock_1 ();  // open: out
  ADD_SUB add_sub_1 (
    .ALU_L(add_sub_1_alu_l), .IRin(IRin), .R1(add_sub_1_r1), .ALU_O(add_sub_1_alu_o),
    .ALU_R(add_sub_1_alu_r), .Actv(or_1_out), .R0(add_sub_1_r0), .ALU_EXE(add_sub_1_alu_exe),
    .R_W(add_sub_1_r_w), .DONE(add_sub_1_done));
  buf buffer_1 (buffer_1_out, add_sub_1_done);
  buf buffer_2 (R_W, add_sub_1_r_w);
  or or_2 (or_2_out, op_rom_1_beq, op_rom_1_bnq);
  buf buffer_3 (Reg0, add_sub_1_r0);
  buf buffer_4 (Reg1, add_sub_1_r1);
  buf buffer_5 (ALU_L, add_sub_1_alu_l);
  buf buffer_6 (ALU_R, add_sub_1_alu_r);
  buf buffer_7 (ALU_O, add_sub_1_alu_o);
  buf buffer_8 (ALU_EXE, add_sub_1_alu_exe);
  buf buffer_9 (ALU_FLAG, op_rom_1_sub);
  T_Flip_Flop t_ff_1 (.T(1'b1), .clk(or_3_out), .Q(t_ff_1_q), .Qn(t_ff_1_qn));  // open: reset, preset
  or or_3 (or_3_out, in_2, buffer_1_out);
  LD ld_1 (
    .AR_I(ld_1_ar_i), .R0_I(ld_1_r0_i), .MBR_I(ld_1_mbr_i), .DONE(ld_1_done), .MBR_O(ld_1_mbr_o),
    .RAM_A(ld_1_ram_a), .ACTV(op_rom_1_ld), .MAR_I(ld_1_mar_i), .MAR_O(ld_1_mar_o), .IR_I(IRin),
    .DR_O(ld_1_dr_o), .R1_I(ld_1_r1_i), .RAM_R(ld_1_ram_r));
  buf buffer_10 (buffer_1_out, ld_1_done);
  buf buffer_11 (R_W, ld_1_r0_i);
  buf buffer_12 (Reg0, ld_1_r0_i);
  buf buffer_13 (Reg1, ld_1_r1_i);
  buf buffer_14 (R_W, ld_1_r1_i);
  buf buffer_15 (MBR_IN, ld_1_mbr_i);
  buf buffer_16 (MBR_OUT, ld_1_mbr_o);
  buf buffer_17 (DR_OUT, ld_1_dr_o);
  buf buffer_18 (AR_IN, ld_1_ar_i);
  buf buffer_19 (RAM_R, ld_1_ram_r);
  buf buffer_20 (MAR_IN, ld_1_mar_i);
  buf buffer_21 (MAR_OUT, ld_1_mar_o);
  assign RAM_A = ld_1_ram_a;  // Buffer buffer_22, 4 bits wide
  SAV sav_1 (
    .R0_OUT(sav_1_r0_out), .MAR_IN(sav_1_mar_in), .MAR_OUT(sav_1_mar_out), .DONE(sav_1_done),
    .R1_OUT(sav_1_r1_out), .IR_IN(IRin), .ACTV(op_rom_1_sav), .AR_IN(sav_1_ar_in), .MBR_IN(sav_1_mbr_in),
    .RAM_W(sav_1_ram_w), .RAM_A(sav_1_ram_a), .DR_IN(sav_1_dr_in), .MBR_OUT(sav_1_mbr_out));
  buf buffer_23 (buffer_1_out, sav_1_done);
  buf buffer_24 (MBR_OUT, sav_1_mbr_out);
  buf buffer_25 (DR_IN, sav_1_dr_in);
  buf buffer_26 (RAM_W, sav_1_ram_w);
  buf buffer_27 (Reg0, sav_1_r0_out);
  buf buffer_28 (Reg1, sav_1_r1_out);
  buf buffer_29 (MAR_IN, sav_1_mar_in);
  buf buffer_30 (MAR_OUT, sav_1_mar_out);
  buf buffer_31 (MBR_IN, sav_1_mbr_in);
  buf buffer_32 (AR_IN, sav_1_ar_in);
  assign RAM_A = sav_1_ram_a;  // Buffer buffer_33, 4 bits wide
  BNQ_BEQ bnq_beq_1 (
    .ALU_R(bnq_beq_1_alu_r), .R0(bnq_beq_1_r0), .ALU_L(bnq_beq_1_alu_l), .PC_A_I(bnq_beq_1_pc_a_i),
    .STAT(bnq_beq_1_stat), .R1(bnq_beq_1_r1), .IRin(IRin), .ALUE_EXE(bnq_beq_1_alue_exe),
    .DONE(bnq_beq_1_done), .Actv(or_2_out), .PC_A_O(bnq_beq_1_pc_a_o));
  buf buffer_34 (buffer_1_out, bnq_beq_1_done);
  buf buffer_35 (ALU_R, bnq_beq_1_alu_r);
  buf buffer_36 (ALU_EXE, bnq_beq_1_alue_exe);
  buf buffer_37 (STAT, bnq_beq_1_stat);
  buf buffer_38 (PC_A_I, bnq_beq_1_pc_a_i);
  assign PC_A_O = bnq_beq_1_pc_a_o;  // Buffer buffer_39, 4 bits wide
  buf buffer_40 (Reg0, bnq_beq_1_r0);
  buf buffer_41 (Reg1, bnq_beq_1_r1);
  buf buffer_42 (ALU_L, bnq_beq_1_alu_l);
  buf buffer_43 (BRANCH_SIGN, op_rom_1_bnq);
  PRT prt_1 (
    .DISP(prt_1_disp), .R0_O(prt_1_r0_o), .IR_I(IRin), .MBR_I(prt_1_mbr_i), .MBR_O(prt_1_mbr_o),
    .R1_O(prt_1_r1_o), .ACTV(op_rom_1_prt), .DONE(prt_1_done));
  buf buffer_44 (buffer_1_out, prt_1_done);
  buf buffer_45 (MBR_OUT, prt_1_mbr_o);
  buf buffer_46 (PNT, prt_1_disp);
  FETCH fetch_1 (
    .MBR_O(fetch_1_mbr_o), .ACTV(t_ff_1_qn), .AR(fetch_1_ar), .PC_O(fetch_1_pc_o), .IR(fetch_1_ir),
    .MBR_I(fetch_1_mbr_i), .MAR_I(fetch_1_mar_i), .DR_O(fetch_1_dr_o), .MAR_O(fetch_1_mar_o),
    .PC_INC(fetch_1_pc_inc), .DONE(fetch_1_done), .RAM_R(fetch_1_ram_r));
  buf buffer_47 (Reg0, prt_1_r0_o);
  buf buffer_48 (Reg1, prt_1_r1_o);
  buf buffer_49 (MBR_IN, prt_1_mbr_i);
  INP inp_1 (
    .R0_I(inp_1_r0_i), .DONE(inp_1_done), .MBR_O(inp_1_mbr_o), .MBR_I(inp_1_mbr_i), .INPT(inp_1_inpt),
    .ACTV(op_rom_1_inp), .IR_I(IRin), .R1_I(inp_1_r1_i));
  buf buffer_50 (buffer_1_out, inp_1_done);
  buf buffer_51 (Reg0, inp_1_r0_i);
  buf buffer_52 (Reg1, inp_1_r1_i);
  buf buffer_53 (R_W, inp_1_r1_i);
  buf buffer_54 (R_W, inp_1_r0_i);
  buf buffer_55 (MAR_OUT, inp_1_mbr_o);
  buf buffer_56 (buffer_1_out, fetch_1_done);
  buf buffer_57 (MAR_IN, inp_1_mbr_i);
  buf buffer_58 (PC_INC, fetch_1_pc_inc);
  buf buffer_59 (INPT, inp_1_inpt);
  buf buffer_60 (MAR_OUT, fetch_1_mar_o);
  buf buffer_61 (MBR_IN, fetch_1_mbr_i);
  buf buffer_62 (MBR_OUT, fetch_1_mbr_o);
  buf buffer_63 (IR, fetch_1_ir);
  buf buffer_64 (PC_OUT, fetch_1_pc_o);
  buf buffer_65 (DR_OUT, fetch_1_dr_o);
  buf buffer_66 (AR_IN, fetch_1_ar);
  buf buffer_67 (RAM_R, fetch_1_ram_r);
  buf buffer_68 (MAR_IN, fetch_1_mar_i);

  // Notes on the sheet:
  //   Control Gates
endmodule

module ADD_SUB (
  input  [7:0] IRin,
  input  Actv,
  output R0,
  output R1,
  output ALU_L,
  output ALU_R,
  output ALU_EXE,
  output ALU_O,
  output R_W,
  output DONE
);

  wire and_1_out, and_2_out, clock_1_out, not_1_out, not_2_out, not_3_out, not_4_out, not_5_out, not_6_out,
       not_7_out, or_1_out, or_2_out, or_3_out, or_4_out, RESET_out, t_ff_1_q, t_ff_1_qn, t_ff_2_q,
       t_ff_2_qn, t_ff_3_q;

  T_Flip_Flop t_ff_1 (
    .T(or_1_out), .clk(clock_1_out), .Q(t_ff_1_q), .Qn(t_ff_1_qn), .reset(RESET_out));  // open: preset
  or or_1 (or_1_out, Actv, ALU_O);
  Clock clock_1 (.out(clock_1_out));
  T_Flip_Flop t_ff_2 (.T(or_1_out), .clk(t_ff_1_qn), .Q(t_ff_2_q), .Qn(t_ff_2_qn), .reset(RESET_out));  // open: preset
  T_Flip_Flop t_ff_3 (.T(or_1_out), .clk(t_ff_2_qn), .Q(t_ff_3_q), .reset(RESET_out));  // open: Qn, preset
  and LOAD1 (ALU_L, t_ff_1_q, not_1_out, not_2_out);
  not not_1 (not_1_out, t_ff_2_q);
  not not_2 (not_2_out, t_ff_3_q);
  not not_3 (not_3_out, t_ff_1_q);
  and LOAD2 (ALU_R, not_3_out, t_ff_2_q, not_4_out);
  not not_4 (not_4_out, t_ff_3_q);
  and EXE (ALU_EXE, t_ff_1_q, t_ff_2_q, not_5_out);
  not not_5 (not_5_out, t_ff_3_q);
  not not_6 (not_6_out, t_ff_1_q);
  not not_7 (not_7_out, t_ff_2_q);
  and SAVE (ALU_O, not_6_out, not_7_out, t_ff_3_q);
  and RESET (RESET_out, t_ff_1_q, t_ff_3_q);
  // NOT_Gate not_8 has open pins: in=t_ff_2_q, out=open
  or or_2 (or_2_out, ALU_O, ALU_L);
  and and_1 (and_1_out, IRin[1], ALU_R);
  and and_2 (and_2_out, IRin[2], or_2_out);
  or or_3 (or_3_out, and_2_out, and_1_out);
  Demultiplexer #(.enable("false")) demultiplexer_1 (.out0(R0), .out1(R1), .in(or_4_out), .sel(or_3_out));
  or or_4 (or_4_out, or_2_out, ALU_R);

  assign DONE = ALU_O;
  assign R_W = ALU_O;
endmodule

module BNQ_BEQ (
  input  [7:0] IRin,
  input  Actv,
  output [3:0] PC_A_O,
  output R0,
  output R1,
  output ALU_L,
  output ALU_R,
  output ALUE_EXE,
  output STAT,
  output PC_A_I,
  output DONE
);

  wire and_1_out, and_2_out, clock_1_out, not_1_out, not_2_out, not_3_out, not_4_out, not_5_out, not_6_out,
       not_7_out, not_8_out, or_1_out, or_2_out, or_3_out, or_4_out, RESET_out, t_ff_1_q, t_ff_1_qn,
       t_ff_2_q, t_ff_2_qn, t_ff_3_q;

  T_Flip_Flop t_ff_1 (
    .T(or_1_out), .clk(clock_1_out), .Q(t_ff_1_q), .Qn(t_ff_1_qn), .reset(RESET_out));  // open: preset
  or or_1 (or_1_out, Actv, DONE);
  Clock clock_1 (.out(clock_1_out));
  T_Flip_Flop t_ff_2 (.T(or_1_out), .clk(t_ff_1_qn), .Q(t_ff_2_q), .Qn(t_ff_2_qn), .reset(RESET_out));  // open: preset
  T_Flip_Flop t_ff_3 (.T(or_1_out), .clk(t_ff_2_qn), .Q(t_ff_3_q), .reset(RESET_out));  // open: Qn, preset
  not not_1 (not_1_out, t_ff_2_q);
  and LOAD1 (ALU_L, t_ff_1_q, not_1_out, not_2_out);
  not not_2 (not_2_out, t_ff_3_q);
  not not_3 (not_3_out, t_ff_1_q);
  and LOAD2 (ALU_R, not_3_out, t_ff_2_q, not_4_out);
  not not_4 (not_4_out, t_ff_3_q);
  and EXE1 (ALUE_EXE, t_ff_1_q, t_ff_2_q, not_5_out);
  not not_5 (not_5_out, t_ff_3_q);
  not not_6 (not_6_out, t_ff_1_q);
  and EXE2 (DONE, not_6_out, not_7_out, t_ff_3_q);
  not not_7 (not_7_out, t_ff_2_q);
  not not_8 (not_8_out, t_ff_2_q);
  and RESET (RESET_out, t_ff_1_q, not_8_out, t_ff_3_q);
  or or_2 (or_2_out, DONE, ALU_L);
  and and_1 (and_1_out, IRin[4], ALU_R);
  and and_2 (and_2_out, IRin[5], or_2_out);
  and and_3 (PC_A_O[0], IRin[0], DONE);
  and and_4 (PC_A_O[1], IRin[1], DONE);
  and and_5 (PC_A_O[2], IRin[2], DONE);
  and and_6 (PC_A_O[3], IRin[3], DONE);
  or or_3 (or_3_out, and_2_out, and_1_out);
  or or_4 (or_4_out, or_2_out, ALU_R);
  Demultiplexer #(.enable("false")) demultiplexer_1 (.out0(R0), .out1(R1), .in(or_4_out), .sel(or_3_out));

  assign PC_A_I = DONE;
  assign STAT = DONE;
endmodule

module FETCH (
  input  ACTV,
  output MAR_I,
  output PC_O,
  output MAR_O,
  output AR,
  output RAM_R,
  output MBR_I,
  output DR_O,
  output MBR_O,
  output IR,
  output PC_INC,
  output DONE
);

  wire and_7_out, clock_1_out, not_1_out, not_2_out, not_3_out, not_4_out, not_5_out, not_6_out, not_7_out,
       not_9_out, or_1_out, t_ff_1_q, t_ff_1_qn, t_ff_2_q, t_ff_2_qn, t_ff_3_q;

  T_Flip_Flop t_ff_1 (
    .T(or_1_out), .clk(clock_1_out), .Q(t_ff_1_q), .Qn(t_ff_1_qn), .reset(and_7_out));  // open: preset
  or or_1 (or_1_out, ACTV, DONE);
  Clock clock_1 (.out(clock_1_out));
  T_Flip_Flop t_ff_2 (.T(or_1_out), .clk(t_ff_1_qn), .Q(t_ff_2_q), .Qn(t_ff_2_qn), .reset(and_7_out));  // open: preset
  T_Flip_Flop t_ff_3 (.T(or_1_out), .clk(t_ff_2_qn), .Q(t_ff_3_q), .reset(and_7_out));  // open: Qn, preset
  and and_1 (MAR_I, t_ff_1_q, not_1_out, not_2_out);
  not not_1 (not_1_out, t_ff_2_q);
  not not_2 (not_2_out, t_ff_3_q);
  not not_3 (not_3_out, t_ff_1_q);
  and and_2 (AR, not_3_out, t_ff_2_q, not_4_out);
  not not_4 (not_4_out, t_ff_3_q);
  and and_3 (RAM_R, t_ff_1_q, t_ff_2_q, not_5_out);
  not not_5 (not_5_out, t_ff_3_q);
  not not_6 (not_6_out, t_ff_1_q);
  and and_4 (DR_O, not_6_out, not_7_out, t_ff_3_q);
  not not_7 (not_7_out, t_ff_2_q);
  and and_5 (IR, t_ff_1_q, t_ff_3_q);
  // NOT_Gate not_8 has open pins: in=t_ff_2_q, out=open
  not not_9 (not_9_out, t_ff_1_q);
  and and_6 (DONE, not_9_out, t_ff_2_q, t_ff_3_q);
  and and_7 (and_7_out, t_ff_1_q, t_ff_2_q, t_ff_3_q);

  assign MAR_O = AR;
  assign MBR_I = DR_O;
  assign MBR_O = IR;
  assign PC_INC = DONE;
  assign PC_O = MAR_I;
endmodule

module SAV (
  input  [7:0] IR_IN,
  input  ACTV,
  output [3:0] RAM_A,
  output MAR_IN,
  output AR_IN,
  output MAR_OUT,
  output MBR_IN,
  output R0_OUT,
  output R1_OUT,
  output MBR_OUT,
  output DR_IN,
  output RAM_W,
  output DONE
);

  wire and_6_out, clock_1_out, not_1_out, not_2_out, not_3_out, not_4_out, not_5_out, not_6_out, not_7_out,
       not_8_out, not_9_out, or_1_out, t_ff_1_q, t_ff_1_qn, t_ff_2_q, t_ff_2_qn, t_ff_3_q;

  T_Flip_Flop t_ff_1 (
    .T(or_1_out), .clk(clock_1_out), .Q(t_ff_1_q), .Qn(t_ff_1_qn), .reset(and_6_out));  // open: preset
  or or_1 (or_1_out, ACTV, DONE);
  Clock clock_1 (.out(clock_1_out));
  T_Flip_Flop t_ff_2 (.T(or_1_out), .clk(t_ff_1_qn), .Q(t_ff_2_q), .Qn(t_ff_2_qn), .reset(and_6_out));  // open: preset
  T_Flip_Flop t_ff_3 (.T(or_1_out), .clk(t_ff_2_qn), .Q(t_ff_3_q), .reset(and_6_out));  // open: Qn, preset
  not not_1 (not_1_out, t_ff_2_q);
  and and_1 (MAR_IN, t_ff_1_q, not_1_out, not_2_out);
  not not_2 (not_2_out, t_ff_3_q);
  not not_3 (not_3_out, t_ff_1_q);
  and and_2 (AR_IN, not_3_out, t_ff_2_q, not_4_out);
  not not_4 (not_4_out, t_ff_3_q);
  and and_3 (MBR_IN, t_ff_1_q, t_ff_2_q, not_5_out);
  not not_5 (not_5_out, t_ff_3_q);
  not not_6 (not_6_out, t_ff_1_q);
  and and_4 (DR_IN, not_6_out, not_7_out, t_ff_3_q);
  not not_7 (not_7_out, t_ff_2_q);
  and and_5 (DONE, t_ff_1_q, not_8_out, t_ff_3_q);
  not not_8 (not_8_out, t_ff_2_q);
  not not_9 (not_9_out, t_ff_1_q);
  and and_6 (and_6_out, not_9_out, t_ff_2_q, t_ff_3_q);
  and and_7 (RAM_A[0], IR_IN[0], MAR_IN);
  and and_8 (RAM_A[1], IR_IN[1], MAR_IN);
  and and_9 (RAM_A[2], IR_IN[2], MAR_IN);
  and and_10 (RAM_A[3], IR_IN[3], MAR_IN);
  Demultiplexer #(.enable("false")) demultiplexer_1 (.out0(R0_OUT), .out1(R1_OUT), .in(MBR_IN), .sel(IR_IN[4]));

  assign MAR_OUT = AR_IN;
  assign MBR_OUT = DR_IN;
  assign RAM_W = DONE;
endmodule

module LD (
  input  [7:0] IR_I,
  input  ACTV,
  output [3:0] RAM_A,
  output MAR_I,
  output MAR_O,
  output AR_I,
  output RAM_R,
  output DR_O,
  output MBR_I,
  output MBR_O,
  output R0_I,
  output R1_I,
  output DONE
);

  wire and_6_out, clock_1_out, not_1_out, not_2_out, not_3_out, not_4_out, not_5_out, not_6_out, not_7_out,
       not_8_out, not_9_out, or_1_out, t_ff_1_q, t_ff_1_qn, t_ff_2_q, t_ff_2_qn, t_ff_3_q;

  T_Flip_Flop t_ff_1 (
    .T(or_1_out), .clk(clock_1_out), .Q(t_ff_1_q), .Qn(t_ff_1_qn), .reset(and_6_out));  // open: preset
  or or_1 (or_1_out, ACTV, DONE);
  Clock clock_1 (.out(clock_1_out));
  T_Flip_Flop t_ff_2 (.T(or_1_out), .clk(t_ff_1_qn), .Q(t_ff_2_q), .Qn(t_ff_2_qn), .reset(and_6_out));  // open: preset
  T_Flip_Flop t_ff_3 (.T(or_1_out), .clk(t_ff_2_qn), .Q(t_ff_3_q), .reset(and_6_out));  // open: Qn, preset
  and and_1 (MAR_I, t_ff_1_q, not_1_out, not_2_out);
  not not_1 (not_1_out, t_ff_2_q);
  not not_2 (not_2_out, t_ff_3_q);
  not not_3 (not_3_out, t_ff_1_q);
  and and_2 (AR_I, not_3_out, t_ff_2_q, not_4_out);
  not not_4 (not_4_out, t_ff_3_q);
  and and_3 (RAM_R, t_ff_1_q, t_ff_2_q, not_5_out);
  not not_5 (not_5_out, t_ff_3_q);
  not not_6 (not_6_out, t_ff_1_q);
  not not_7 (not_7_out, t_ff_2_q);
  and and_4 (DR_O, not_6_out, not_7_out, t_ff_3_q);
  not not_8 (not_8_out, t_ff_2_q);
  and and_5 (DONE, t_ff_1_q, not_8_out, t_ff_3_q);
  not not_9 (not_9_out, t_ff_1_q);
  and and_6 (and_6_out, not_9_out, t_ff_2_q, t_ff_3_q);
  and and_7 (RAM_A[0], IR_I[0], MAR_I);
  and and_8 (RAM_A[1], IR_I[1], MAR_I);
  and and_9 (RAM_A[2], IR_I[2], MAR_I);
  and and_10 (RAM_A[3], IR_I[3], MAR_I);
  Demultiplexer #(.enable("false")) demultiplexer_1 (.out0(R0_I), .out1(R1_I), .in(DONE), .sel(IR_I[4]));

  assign MAR_O = AR_I;
  assign MBR_I = DR_O;
  assign MBR_O = DONE;
endmodule

module PRT (
  input  [7:0] IR_I,
  input  ACTV,
  output MBR_I,
  output R0_O,
  output R1_O,
  output MBR_O,
  output DISP,
  output DONE
);

  wire and_3_out, clock_1_out, not_1_out, not_2_out, not_3_out, not_4_out, not_5_out, or_1_out, t_ff_1_q,
       t_ff_1_qn, t_ff_2_q, t_ff_2_qn, t_ff_3_q;

  T_Flip_Flop t_ff_1 (
    .T(or_1_out), .clk(clock_1_out), .Q(t_ff_1_q), .Qn(t_ff_1_qn), .reset(and_3_out));  // open: preset
  or or_1 (or_1_out, ACTV, DISP);
  Clock clock_1 (.out(clock_1_out));
  T_Flip_Flop t_ff_2 (.T(or_1_out), .clk(t_ff_1_qn), .Q(t_ff_2_q), .Qn(t_ff_2_qn), .reset(and_3_out));  // open: preset
  T_Flip_Flop t_ff_3 (.T(or_1_out), .clk(t_ff_2_qn), .Q(t_ff_3_q), .reset(and_3_out));  // open: Qn, preset
  and and_1 (MBR_I, t_ff_1_q, not_1_out, not_2_out);
  not not_1 (not_1_out, t_ff_2_q);
  not not_2 (not_2_out, t_ff_3_q);
  not not_3 (not_3_out, t_ff_1_q);
  and and_2 (DISP, not_3_out, t_ff_2_q, not_4_out);
  not not_4 (not_4_out, t_ff_3_q);
  and and_3 (and_3_out, t_ff_1_q, t_ff_2_q, not_5_out);
  not not_5 (not_5_out, t_ff_3_q);
  Demultiplexer #(.enable("false")) demultiplexer_1 (.out0(R0_O), .out1(R1_O), .in(MBR_I), .sel(IR_I[1]));

  assign DONE = DISP;
  assign MBR_O = DISP;
endmodule

module INP (
  input  [7:0] IR_I,
  input  ACTV,
  output INPT,
  output MBR_I,
  output MBR_O,
  output DONE,
  output R0_I,
  output R1_I
);

  wire and_3_out, clock_1_out, not_1_out, not_2_out, or_1_out, t_ff_1_q, t_ff_1_qn, t_ff_2_q;

  T_Flip_Flop t_ff_1 (
    .T(or_1_out), .clk(clock_1_out), .Q(t_ff_1_q), .Qn(t_ff_1_qn), .reset(and_3_out));  // open: preset
  or or_1 (or_1_out, ACTV, DONE);
  Clock clock_1 (.out(clock_1_out));
  T_Flip_Flop t_ff_2 (.T(or_1_out), .clk(t_ff_1_qn), .Q(t_ff_2_q), .reset(and_3_out));  // open: Qn, preset
  and and_1 (INPT, t_ff_1_q, not_1_out);
  not not_1 (not_1_out, t_ff_2_q);
  not not_2 (not_2_out, t_ff_1_q);
  and and_2 (DONE, not_2_out, t_ff_2_q);
  and and_3 (and_3_out, t_ff_1_q, t_ff_2_q);
  Demultiplexer #(.enable("false")) demultiplexer_1 (.out0(R0_I), .out1(R1_I), .in(DONE), .sel(IR_I[1]));

  assign MBR_I = INPT;
  assign MBR_O = DONE;
endmodule
